// Logisim project 实验2-CS1804-U201814755-彭子晨.circ as structural Verilog: 10 circuits, main circuit 四位二进制可逆计数器
module \四位二进制可逆计数器  (
  input  CLR,
  input  nDL,
  input  CPu,
  input  CPd,
  input  A,
  input  B,
  input  C,
  input  D,
  output Qa,
  output Qb,
  output Qc,
  output Qd
);

  wire and_1_out, and_2_out, and_3_out, and_4_out, and_5_out, and_6_out, and_7_out, and_8_out, and_9_out,
       and_10_out, and_11_out, and_12_out, and_13_out, and_14_out, d_ff_1_qn, d_ff_2_qn, d_ff_3_qn,
       d_ff_4_qn, not_1_out, not_2_out, not_3_out, not_4_out, not_5_out, not_6_out, not_7_out, not_8_out,
       not_9_out, not_10_out, not_11_out, or_1_out, or_2_out, or_3_out, or_4_out, or_5_out, or_6_out,
       or_7_out, or_8_out;

  not not_1 (not_1_out, Qa);
  not not_2 (not_2_out, Qa);
  not not_3 (not_3_out, Qb);
  not not_4 (not_4_out, Qa);
  not not_5 (not_5_out, Qb);
  not not_6 (not_6_out, Qc);
  or or_1 (or_1_out, CPu, CPd);
  and and_1 (and_1_out, CPu, Qa);
  and and_2 (and_2_out, CPd, not_1_out);
  and and_3 (and_3_out, CPu, Qa, Qb);
  or or_2 (or_2_out, and_3_out, and_4_out);
  and and_4 (and_4_out, CPd, not_2_out, not_3_out);
  and and_5 (and_5_out, CPu, Qa, Qb, Qc);
  or or_3 (or_3_out, and_5_out, and_6_out);
  and and_6 (and_6_out, CPd, not_4_out, not_5_out, not_6_out);
  D_Flip_Flop #(.trigger("falling")) d_ff_1 (
    .clk(or_1_out), .D(d_ff_1_qn), .Q(Qa), .Qn(d_ff_1_qn), .preset(and_7_out), .reset(or_4_out));  // open: en
  or or_4 (or_4_out, CLR, and_8_out);
  or or_5 (or_5_out, and_1_out, and_2_out);
  D_Flip_Flop #(.trigger("falling")) d_ff_2 (
    .clk(or_5_out), .D(d_ff_2_qn), .Q(Qb), .Qn(d_ff_2_qn), .preset(and_9_out), .reset(or_6_out));  // open: en
  or or_6 (or_6_out, CLR, and_10_out);
  D_Flip_Flop #(.trigger("falling")) d_ff_3 (
    .clk(or_2_out), .D(d_ff_3_qn), .Q(Qc), .Qn(d_ff_3_qn), .preset(and_11_out), .reset(or_7_out));  // open: en
  or or_7 (or_7_out, CLR, and_12_out);
  D_Flip_Flop #(.trigger("falling")) d_ff_4 (
    .clk(or_3_out), .D(d_ff_4_qn), .Q(Qd), .Qn(d_ff_4_qn), .preset(and_13_out), .reset(or_8_out));  // open: en
  or or_8 (or_8_out, CLR, and_14_out);
  not not_7 (not_7_out, nDL);
  and and_7 (and_7_out, A, not_7_out);
  and and_8 (and_8_out, not_8_out, not_7_out);
  and and_9 (and_9_out, B, not_7_out);
  and and_10 (and_10_out, not_9_out, not_7_out);
  and and_11 (and_11_out, C, not_7_out);
  and and_12 (and_12_out, not_10_out, not_7_out);
  and and_13 (and_13_out, D, not_7_out);
  and and_14 (and_14_out, not_11_out, not_7_out);
  not not_8 (not_8_out, A);
  not not_9 (not_9_out, B);
  not not_10 (not_10_out, C);
  not not_11 (not_11_out, D);
endmodule

module \四位二进制可逆计数器测试电路  (
  input  in_1,
  input  in_2,
  input  in_3,
  input  in_4,
  input  in_5,
  input  in_6,
  input  in_7,
  input  in_8,
  output out_9,
  output out_10,
  output out_11,
  output out_12
);

  \四位二进制可逆计数器  \u_四位二进制可逆计数器_1  (
    .CPu(in_1), .CPd(in_3), .Qa(out_12), .A(in_7), .Qb(out_11), .B(in_6), .Qc(out_10), .C(in_5), .Qd(out_9),
    .D(in_4), .CLR(in_2), .nDL(in_8));
endmodule

module \二进制转8421码电路  (
  input  A3,
  input  A2,
  input  A1,
  input  A0,
  output S80,
  output S40,
  output S20,
  output S8,
  output S4,
  output S2,
  output S1,
  output S10
);

  wire and_1_out, or_1_out;

  \先行进位的四位二进制并行加法器  \u_先行进位的四位二进制并行加法器_1  (
    .A0(A0), .B0(1'b0), .A1(A1), .B1(and_1_out), .A2(A2), .B2(and_1_out), .A3(A3), .B3(1'b0), .S0(S1),
    .S1(S2), .S2(S4), .S3(S8), .C4(S10), .C0(1'b0));
  and and_1 (and_1_out, A3, or_1_out);
  or or_1 (or_1_out, A2, A1);

  assign S20 = 1'b0;
  assign S40 = 1'b0;
  assign S80 = 1'b0;
endmodule

module \二进制转8421码测试电路  (
  input  in_1,
  input  in_2,
  input  in_3,
  input  in_4,
  output out_5,
  output out_6,
  output out_7,
  output out_8,
  output out_9,
  output out_10,
  output out_11,
  output out_12
);

  \二进制转8421码电路  \u_二进制转8421码电路_1  (
    .S8(out_9), .S4(out_10), .S2(out_11), .S1(out_12), .S10(out_8), .A3(in_1), .A2(in_2), .A1(in_3),
    .A0(in_4), .S20(out_7), .S40(out_6), .S80(out_5));
endmodule

module \显示电路  (
  input  A3,
  input  A2,
  input  A1,
  input  A0,
  output a,
  output b,
  output c,
  output d,
  output e,
  output f,
  output g
);

  wire and_1_out, and_2_out, and_3_out, and_4_out, and_5_out, and_6_out, and_7_out, and_8_out, and_9_out,
       and_10_out, and_11_out, and_12_out, and_13_out, and_14_out, and_15_out, and_16_out, and_17_out,
       and_18_out, and_19_out, and_20_out, and_21_out, and_22_out, and_23_out, and_24_out, and_25_out,
       not_1_out, not_2_out, not_3_out, not_4_out;

  not not_1 (not_1_out, A3);
  not not_2 (not_2_out, A2);
  not not_3 (not_3_out, A1);
  not not_4 (not_4_out, A0);
  and and_1 (and_1_out, not_2_out, not_3_out, not_4_out);
  and and_2 (and_2_out, not_1_out, not_2_out, A1);
  and and_3 (and_3_out, not_1_out, A2, A0);
  and and_4 (and_4_out, A3, not_3_out, A0);
  and and_5 (and_5_out, not_1_out, not_2_out);
  and and_6 (and_6_out, not_3_out, not_4_out);
  and and_7 (and_7_out, not_2_out, not_3_out);
  and and_8 (and_8_out, not_1_out, A1, A0);
  and and_9 (and_9_out, not_1_out, A2);
  and and_10 (and_10_out, not_2_out, not_3_out);
  and and_11 (and_11_out, not_2_out, A0);
  and and_12 (and_12_out, A2, not_3_out, A0);
  and and_13 (and_13_out, not_2_out, not_4_out);
  and and_14 (and_14_out, not_2_out, A1, A0);
  and and_15 (and_15_out, A2, A1, not_4_out);
  and and_16 (and_16_out, A1, not_4_out);
  and and_17 (and_17_out, not_2_out, not_4_out);
  and and_18 (and_18_out, not_3_out, not_4_out);
  and and_19 (and_19_out, A2, not_3_out);
  and and_20 (and_20_out, A3, not_2_out, not_3_out);
  and and_21 (and_21_out, A2, not_4_out);
  and and_22 (and_22_out, A2, not_3_out);
  and and_23 (and_23_out, A3, not_2_out);
  and and_24 (and_24_out, not_2_out, A1);
  and and_25 (and_25_out, A1, not_4_out);
  or or_1 (a, and_1_out, and_2_out, and_3_out, and_4_out);
  or or_2 (b, and_5_out, and_6_out, and_7_out, and_8_out);
  or or_3 (c, and_9_out, and_10_out, and_11_out);
  or or_4 (d, and_12_out, and_13_out, and_14_out, and_15_out);
  or or_5 (e, and_16_out, and_17_out);
  or or_6 (f, and_18_out, and_19_out, and_20_out, and_21_out);
  or or_7 (g, and_22_out, and_23_out, and_24_out, and_25_out);
endmodule

module \显示电路测试电路  (
  input  in_1,
  input  in_2,
  input  in_3,
  input  in_4,
  output out_5,
  output out_6,
  output out_7,
  output out_8,
  output out_9,
  output out_10,
  output out_11,
  output out_12,
  output out_13,
  output out_14,
  output out_15,
  output out_16,
  output out_17,
  output out_18
);

  \显示电路  \u_显示电路_1  (
    .A3(in_1), .A2(in_2), .A1(in_3), .A0(in_4), .a(out_5), .b(out_8), .c(out_14), .d(out_17), .e(out_13),
    .f(out_7), .g(out_11));

  assign out_6 = out_5;
  assign out_9 = out_7;
  assign out_10 = out_8;
  assign out_12 = out_11;
  assign out_15 = out_13;
  assign out_16 = out_14;
  assign out_18 = out_17;
endmodule

module \报警电路  (
  input  \进入 ,
  input  CLR,
  input  \出门 ,
  input  A3,
  input  A2,
  input  A1,
  input  A0,
  output out_8,
  output out_9,
  output out_10,
  output out_11,
  output out_12,
  output out_13,
  output out_14,
  output out_15
);

  wire and_1_out, and_2_out, and_3_out, and_4_out, and_5_out, not_1_out, not_2_out, not_3_out, not_4_out,
       not_5_out, not_6_out, \四位二进制可逆计数器_1_qa , \四位二进制可逆计数器_1_qb , \四位二进制可逆计数器_1_qc , \四位二进制可逆计数器_1_qd ;

  not not_1 (not_1_out, and_4_out);
  and and_1 (and_1_out, not_1_out, \进入 );
  and and_2 (and_2_out, \出门 , not_2_out);
  \二进制转8421码电路  \u_二进制转8421码电路_1  (
    .S8(out_12), .S4(out_13), .S2(out_14), .S1(out_15), .S10(out_11), .A3(\四位二进制可逆计数器_1_qd ),
    .A2(\四位二进制可逆计数器_1_qc ), .A1(\四位二进制可逆计数器_1_qb ), .A0(\四位二进制可逆计数器_1_qa ), .S20(out_10), .S40(out_9),
    .S80(out_8));
  not not_2 (not_2_out, and_3_out);
  \四位二进制可逆计数器  \u_四位二进制可逆计数器_1  (
    .CPu(and_1_out), .CPd(and_2_out), .Qa(\四位二进制可逆计数器_1_qa ), .A(A0), .Qb(\四位二进制可逆计数器_1_qb ), .B(A1),
    .Qc(\四位二进制可逆计数器_1_qc ), .C(A2), .Qd(\四位二进制可逆计数器_1_qd ), .D(A3), .CLR(CLR), .nDL(1'b1));
  not not_3 (not_3_out, \四位二进制可逆计数器_1_qd );
  not not_4 (not_4_out, \四位二进制可逆计数器_1_qc );
  not not_5 (not_5_out, \四位二进制可逆计数器_1_qb );
  not not_6 (not_6_out, \四位二进制可逆计数器_1_qa );
  and and_3 (and_3_out, not_3_out, not_4_out, not_5_out, not_6_out);
  and and_4 (and_4_out, \四位二进制可逆计数器_1_qd , \四位二进制可逆计数器_1_qc , \四位二进制可逆计数器_1_qb , \四位二进制可逆计数器_1_qa );
  and and_5 (and_5_out, and_4_out, \进入 );
  LED \u_报警  (.in(and_5_out));
endmodule

module \小型实验室门禁系统  (
  input  \进入 ,
  input  CLR,
  input  \出门 ,
  output a1,
  output b1,
  output c1,
  output d1,
  output e1,
  output f1,
  output g1,
  output a2,
  output b2,
  output c2,
  output d2,
  output e2,
  output f2,
  output g2,
  output \报警 
);

  wire and_1_out, and_2_out, and_3_out, and_4_out, not_1_out, not_2_out, not_3_out, not_4_out, not_5_out,
       not_6_out, \二进制转8421码电路_1_s1 , \二进制转8421码电路_1_s2 , \二进制转8421码电路_1_s4 , \二进制转8421码电路_1_s8 ,
       \二进制转8421码电路_1_s10 , \二进制转8421码电路_1_s20 , \二进制转8421码电路_1_s40 , \二进制转8421码电路_1_s80 , \四位二进制可逆计数器_1_qa ,
       \四位二进制可逆计数器_1_qb , \四位二进制可逆计数器_1_qc , \四位二进制可逆计数器_1_qd ;

  \显示电路  \u_显示电路_1  (
    .A3(\二进制转8421码电路_1_s80 ), .A2(\二进制转8421码电路_1_s40 ), .A1(\二进制转8421码电路_1_s20 ), .A0(\二进制转8421码电路_1_s10 ),
    .a(a1), .b(b1), .c(c1), .d(d1), .e(e1), .f(f1), .g(g1));
  not not_1 (not_1_out, and_4_out);
  and and_1 (and_1_out, not_1_out, \进入 );
  and and_2 (and_2_out, \出门 , not_2_out);
  \二进制转8421码电路  \u_二进制转8421码电路_1  (
    .S8(\二进制转8421码电路_1_s8 ), .S4(\二进制转8421码电路_1_s4 ), .S2(\二进制转8421码电路_1_s2 ), .S1(\二进制转8421码电路_1_s1 ),
    .S10(\二进制转8421码电路_1_s10 ), .A3(\四位二进制可逆计数器_1_qd ), .A2(\四位二进制可逆计数器_1_qc ), .A1(\四位二进制可逆计数器_1_qb ),
    .A0(\四位二进制可逆计数器_1_qa ), .S20(\二进制转8421码电路_1_s20 ), .S40(\二进制转8421码电路_1_s40 ), .S80(\二进制转8421码电路_1_s80 ));
  not not_2 (not_2_out, and_3_out);
  \四位二进制可逆计数器  \u_四位二进制可逆计数器_1  (
    .CPu(and_1_out), .CPd(and_2_out), .Qa(\四位二进制可逆计数器_1_qa ), .A(1'b0), .Qb(\四位二进制可逆计数器_1_qb ), .B(1'b0),
    .Qc(\四位二进制可逆计数器_1_qc ), .C(1'b0), .Qd(\四位二进制可逆计数器_1_qd ), .D(1'b0), .CLR(CLR), .nDL(1'b1));
  \显示电路  \u_显示电路_2  (
    .A3(\二进制转8421码电路_1_s8 ), .A2(\二进制转8421码电路_1_s4 ), .A1(\二进制转8421码电路_1_s2 ), .A0(\二进制转8421码电路_1_s1 ),
    .a(a2), .b(b2), .c(c2), .d(d2), .e(e2), .f(f2), .g(g2));
  not not_3 (not_3_out, \四位二进制可逆计数器_1_qd );
  not not_4 (not_4_out, \四位二进制可逆计数器_1_qc );
  not not_5 (not_5_out, \四位二进制可逆计数器_1_qb );
  not not_6 (not_6_out, \四位二进制可逆计数器_1_qa );
  and and_3 (and_3_out, not_3_out, not_4_out, not_5_out, not_6_out);
  and and_4 (and_4_out, \四位二进制可逆计数器_1_qd , \四位二进制可逆计数器_1_qc , \四位二进制可逆计数器_1_qb , \四位二进制可逆计数器_1_qa );
  and and_5 (\报警 , and_4_out, \进入 );
endmodule

module \小型门禁系统测试电路  (
  input  in_1,
  input  in_2,
  input  in_3
);

  wire \小型实验室门禁系统_1_a1 , \小型实验室门禁系统_1_a2 , \小型实验室门禁系统_1_b1 , \小型实验室门禁系统_1_b2 , \小型实验室门禁系统_1_c1 ,
       \小型实验室门禁系统_1_c2 , \小型实验室门禁系统_1_d1 , \小型实验室门禁系统_1_d2 , \小型实验室门禁系统_1_e1 , \小型实验室门禁系统_1_e2 ,
       \小型实验室门禁系统_1_f1 , \小型实验室门禁系统_1_f2 , \小型实验室门禁系统_1_g1 , \小型实验室门禁系统_1_g2 , \小型实验室门禁系统_1_报警 ;

  \小型实验室门禁系统  \u_小型实验室门禁系统_1  (
    .\进入 (in_1), .CLR(in_2), .\出门 (in_3), .a1(\小型实验室门禁系统_1_a1 ), .b1(\小型实验室门禁系统_1_b1 ),
    .c1(\小型实验室门禁系统_1_c1 ), .d1(\小型实验室门禁系统_1_d1 ), .e1(\小型实验室门禁系统_1_e1 ), .f1(\小型实验室门禁系统_1_f1 ),
    .g1(\小型实验室门禁系统_1_g1 ), .a2(\小型实验室门禁系统_1_a2 ), .b2(\小型实验室门禁系统_1_b2 ), .c2(\小型实验室门禁系统_1_c2 ),
    .d2(\小型实验室门禁系统_1_d2 ), .e2(\小型实验室门禁系统_1_e2 ), .f2(\小型实验室门禁系统_1_f2 ), .g2(\小型实验室门禁系统_1_g2 ),
    .\报警 (\小型实验室门禁系统_1_报警 ));
  _7_Segment_Display u_7_segment_display_1 (
    .g(\小型实验室门禁系统_1_g1 ), .f(\小型实验室门禁系统_1_f1 ), .a(\小型实验室门禁系统_1_a1 ), .b(\小型实验室门禁系统_1_b1 ),
    .e(\小型实验室门禁系统_1_e1 ), .d(\小型实验室门禁系统_1_d1 ), .c(\小型实验室门禁系统_1_c1 ));  // open: dp
  _7_Segment_Display u_7_segment_display_2 (
    .g(\小型实验室门禁系统_1_g2 ), .f(\小型实验室门禁系统_1_f2 ), .a(\小型实验室门禁系统_1_a2 ), .b(\小型实验室门禁系统_1_b2 ),
    .e(\小型实验室门禁系统_1_e2 ), .d(\小型实验室门禁系统_1_d2 ), .c(\小型实验室门禁系统_1_c2 ));  // open: dp
  LED led_1 (.in(\小型实验室门禁系统_1_报警 ));
endmodule

module \先行进位的四位二进制并行加法器  (
  input  C0,
  input  A0,
  input  B0,
  input  A1,
  input  B1,
  input  A2,
  input  B2,
  input  A3,
  input  B3,
  output S0,
  output S1,
  output S2,
  output S3,
  output C4
);

  wire and_1_out, and_2_out, and_3_out, and_4_out, and_5_out, and_6_out, and_7_out, and_8_out, and_9_out,
       and_10_out, and_11_out, and_12_out, and_13_out, and_14_out, or_1_out, or_2_out, or_3_out, or_4_out,
       or_5_out, or_6_out, or_7_out, xor_1_out, xor_2_out, xor_3_out, xor_4_out;

  or or_1 (or_1_out, A0, B0);
  and and_1 (and_1_out, A0, B0);
  and and_2 (and_2_out, and_1_out, or_4_out, or_2_out);
  or or_2 (or_2_out, A2, B2);
  and and_3 (and_3_out, C0, or_1_out);
  or or_3 (or_3_out, and_3_out, and_1_out);
  and and_4 (and_4_out, B2, A2);
  and and_5 (and_5_out, and_1_out, or_4_out);
  or or_4 (or_4_out, B1, A1);
  and and_6 (and_6_out, B1, A1);
  and and_7 (and_7_out, C0, or_2_out, and_1_out, or_4_out);
  and and_8 (and_8_out, and_6_out, or_2_out);
  and and_9 (and_9_out, C0, or_4_out, or_1_out);
  or or_5 (or_5_out, and_4_out, and_2_out, and_8_out, and_7_out);
  and and_10 (and_10_out, or_2_out, or_6_out, and_6_out);
  and and_11 (and_11_out, A3, B3);
  or or_6 (or_6_out, A3, B3);
  or or_7 (or_7_out, and_5_out, and_9_out, and_6_out);
  and and_12 (and_12_out, or_2_out, or_4_out, and_1_out, or_6_out);
  and and_13 (and_13_out, or_6_out, and_4_out);
  and and_14 (and_14_out, C0, or_1_out, or_4_out, or_2_out, or_6_out);
  xor xor_1 (xor_1_out, A0, B0);
  xor xor_2 (xor_2_out, A1, B1);
  xor xor_3 (xor_3_out, A2, B2);
  xor xor_4 (xor_4_out, A3, B3);
  or or_8 (C4, and_12_out, and_11_out, and_14_out, and_13_out, and_10_out);
  xor xor_5 (S0, xor_1_out, C0);
  xor xor_6 (S1, xor_2_out, or_3_out);
  xor xor_7 (S2, xor_3_out, or_7_out);
  xor xor_8 (S3, xor_4_out, or_5_out);
endmodule
