// Logisim project 实验3-CS1804-U201814755-彭子晨.circ as structural Verilog: 6 circuits, main circuit 四位乘法器
module \四位乘法器  (
  input  [3:0] A,
  input  [3:0] B,
  output [7:0] out_3
);

  wire [7:0] adder_1_out, adder_2_out, adder_3_out, adder_4_out, bit_extender_1_out, multiplexer_1_out,
       multiplexer_2_out, multiplexer_3_out, shifter_1_out, shifter_2_out, shifter_3_out;

  assign bit_extender_1_out = {{4{1'b0}}, B};  // Bit_Extender bit_extender_1
  Adder #(.width(8)) adder_1 (.a({8{1'b0}}), .b(bit_extender_1_out), .out(adder_1_out));  // open: cin, cout
  Multiplexer #(.select(1), .width(8), .disabled("Z"), .enable("false")) multiplexer_1 (
    .in0({8{1'b0}}), .in1(adder_1_out), .out(multiplexer_1_out), .sel(A[0]));
  Shifter #(.width(8), .shift("ll")) shifter_1 (.in(bit_extender_1_out), .\dist (3'b001), .out(shifter_1_out));
  Adder #(.width(8)) adder_2 (.a(multiplexer_1_out), .b(shifter_1_out), .out(adder_2_out));  // open: cin, cout
  Multiplexer #(.select(1), .width(8), .disabled("Z"), .enable("false")) multiplexer_2 (
    .in0(multiplexer_1_out), .in1(adder_2_out), .out(multiplexer_2_out), .sel(A[1]));
  Shifter #(.width(8), .shift("ll")) shifter_2 (.in(shifter_1_out), .\dist (3'b001), .out(shifter_2_out));
  Adder #(.width(8)) adder_3 (.a(multiplexer_2_out), .b(shifter_2_out), .out(adder_3_out));  // open: cin, cout
  Multiplexer #(.select(1), .width(8), .disabled("Z"), .enable("false")) multiplexer_3 (
    .in0(multiplexer_2_out), .in1(adder_3_out), .out(multiplexer_3_out), .sel(A[2]));
  Shifter #(.width(8), .shift("ll")) shifter_3 (.in(shifter_2_out), .\dist (3'b001), .out(shifter_3_out));
  Adder #(.width(8)) adder_4 (.a(multiplexer_3_out), .b(shifter_3_out), .out(adder_4_out));  // open: cin, cout
  Multiplexer #(.select(1), .width(8), .disabled("Z"), .enable("false")) multiplexer_4 (
    .in0(multiplexer_3_out), .in1(adder_4_out), .out(out_3), .sel(A[3]));
endmodule

module \四位乘法器测试电路  (
  input  [3:0] in_1,
  input  [3:0] in_2,
  output [7:0] out_3
);

  \四位乘法器  \u_四位乘法器_1  (.B(in_2), .out_3(out_3), .A(in_1));
endmodule

module \_32X4乘法器  (
  input  [3:0] A,
  input  [31:0] B,
  output [31:0] Ph,
  output [31:0] Pl
);

  wire adder_3_cout, adder_5_cout, adder_7_cout;
  wire [31:0] adder_1_out, adder_2_out, adder_3_out, adder_4_out, adder_5_out, adder_6_out, adder_7_out,
       multiplexer_1_out, multiplexer_2_out, multiplexer_3_out, multiplexer_4_out, multiplexer_5_out,
       shifter_1_out, shifter_2_out, shifter_3_out, shifter_4_out, shifter_5_out, shifter_6_out;

  Shifter #(.width(32), .shift("lr")) shifter_1 (.in(B), .\dist ({5{1'b1}}), .out(shifter_1_out));
  Adder #(.width(32)) adder_1 (.a({32{1'b0}}), .b(shifter_1_out), .out(adder_1_out), .cin(adder_3_cout));  // open: cout
  Multiplexer #(.select(1), .width(32), .disabled("Z"), .enable("false")) multiplexer_1 (
    .in0({32{1'b0}}), .in1(adder_2_out), .out(multiplexer_1_out), .sel(A[0]));
  Adder #(.width(32)) adder_2 (.a({32{1'b0}}), .b(B), .out(adder_2_out));  // open: cin, cout
  Shifter #(.width(32), .shift("ll")) shifter_2 (.in(B), .\dist (5'b00001), .out(shifter_2_out));
  Multiplexer #(.select(1), .width(32), .disabled("Z"), .enable("false")) multiplexer_2 (
    .in0({32{1'b0}}), .in1(adder_1_out), .out(multiplexer_2_out), .sel(A[1]));
  Adder #(.width(32)) adder_3 (
    .a(multiplexer_1_out), .b(shifter_2_out), .out(adder_3_out), .cout(adder_3_cout));  // open: cin
  Shifter #(.width(32), .shift("lr")) shifter_3 (.in(B), .\dist (5'b11110), .out(shifter_3_out));
  Multiplexer #(.select(1), .width(32), .disabled("Z"), .enable("false")) multiplexer_3 (
    .in0(multiplexer_1_out), .in1(adder_3_out), .out(multiplexer_3_out), .sel(A[1]));
  Shifter #(.width(32), .shift("ll")) shifter_4 (.in(shifter_2_out), .\dist (5'b00001), .out(shifter_4_out));
  Adder #(.width(32)) adder_4 (
    .a(multiplexer_2_out), .b(shifter_3_out), .out(adder_4_out), .cin(adder_5_cout));  // open: cout
  Adder #(.width(32)) adder_5 (
    .a(multiplexer_3_out), .b(shifter_4_out), .out(adder_5_out), .cout(adder_5_cout));  // open: cin
  Multiplexer #(.select(1), .width(32), .disabled("Z"), .enable("false")) multiplexer_4 (
    .in0(multiplexer_2_out), .in1(adder_4_out), .out(multiplexer_4_out), .sel(A[2]));
  Multiplexer #(.select(1), .width(32), .disabled("Z"), .enable("false")) multiplexer_5 (
    .in0(multiplexer_3_out), .in1(adder_5_out), .out(multiplexer_5_out), .sel(A[2]));
  Shifter #(.width(32), .shift("ll")) shifter_5 (.in(shifter_4_out), .\dist (5'b00001), .out(shifter_5_out));
  Shifter #(.width(32), .shift("lr")) shifter_6 (.in(B), .\dist (5'b11101), .out(shifter_6_out));
  Multiplexer #(.select(1), .width(32), .disabled("Z"), .enable("false")) multiplexer_6 (
    .in0(multiplexer_4_out), .in1(adder_6_out), .out(Ph), .sel(A[3]));
  Adder #(.width(32)) adder_6 (
    .a(multiplexer_4_out), .b(shifter_6_out), .out(adder_6_out), .cin(adder_7_cout));  // open: cout
  Multiplexer #(.select(1), .width(32), .disabled("Z"), .enable("false")) multiplexer_7 (
    .in0(multiplexer_5_out), .in1(adder_7_out), .out(Pl), .sel(A[3]));
  Adder #(.width(32)) adder_7 (
    .a(multiplexer_5_out), .b(shifter_5_out), .out(adder_7_out), .cout(adder_7_cout));  // open: cin
endmodule

module \_32X4乘法器测试电路  (
  input  [3:0] in_1,
  input  [31:0] in_2,
  output [31:0] out_3,
  output [31:0] out_4
);

  \_32X4乘法器  \u_32x4乘法器_1  (.A(in_1), .B(in_2), .Pl(out_4), .Ph(out_3));
endmodule

module \_32X32乘法器  (
  input  [31:0] A,
  input  [31:0] B,
  output [31:0] Ph,
  output [31:0] Pl
);

  wire adder_1_cout, adder_2_cout, adder_3_cout, adder_4_cout, adder_5_cout, adder_6_cout, adder_7_cout;
  wire [31:0] adder_1_out, adder_2_out, adder_3_out, adder_4_out, adder_5_out, adder_6_out, adder_8_out,
       adder_9_out, adder_10_out, adder_11_out, adder_12_out, adder_13_out, adder_14_out, adder_15_out,
       adder_16_out, adder_17_out, adder_18_out, adder_19_out, adder_20_out, \n32x4乘法器_1_ph ,
       \n32x4乘法器_1_pl , \n32x4乘法器_2_ph , \n32x4乘法器_2_pl , \n32x4乘法器_3_ph , \n32x4乘法器_3_pl , \n32x4乘法器_4_ph ,
       \n32x4乘法器_4_pl , \n32x4乘法器_5_ph , \n32x4乘法器_5_pl , \n32x4乘法器_6_ph , \n32x4乘法器_6_pl , \n32x4乘法器_7_ph ,
       \n32x4乘法器_7_pl , \n32x4乘法器_8_ph , \n32x4乘法器_8_pl , shifter_1_out, shifter_2_out, shifter_3_out,
       shifter_4_out, shifter_5_out, shifter_6_out, shifter_7_out, shifter_8_out, shifter_9_out,
       shifter_10_out, shifter_11_out, shifter_12_out, shifter_13_out, shifter_14_out, shifter_15_out,
       shifter_16_out, shifter_17_out, shifter_18_out, shifter_19_out, shifter_20_out, shifter_21_out;

  \_32X4乘法器  \u_32x4乘法器_1  (.A(A[3:0]), .B(B), .Pl(\n32x4乘法器_1_pl ), .Ph(\n32x4乘法器_1_ph ));
  \_32X4乘法器  \u_32x4乘法器_2  (.A(A[7:4]), .B(B), .Pl(\n32x4乘法器_2_pl ), .Ph(\n32x4乘法器_2_ph ));
  \_32X4乘法器  \u_32x4乘法器_3  (.A(A[11:8]), .B(B), .Pl(\n32x4乘法器_3_pl ), .Ph(\n32x4乘法器_3_ph ));
  \_32X4乘法器  \u_32x4乘法器_4  (.A(A[15:12]), .B(B), .Pl(\n32x4乘法器_4_pl ), .Ph(\n32x4乘法器_4_ph ));
  \_32X4乘法器  \u_32x4乘法器_5  (.A(A[19:16]), .B(B), .Pl(\n32x4乘法器_5_pl ), .Ph(\n32x4乘法器_5_ph ));
  \_32X4乘法器  \u_32x4乘法器_6  (.A(A[23:20]), .B(B), .Pl(\n32x4乘法器_6_pl ), .Ph(\n32x4乘法器_6_ph ));
  \_32X4乘法器  \u_32x4乘法器_7  (.A(A[27:24]), .B(B), .Pl(\n32x4乘法器_7_pl ), .Ph(\n32x4乘法器_7_ph ));
  \_32X4乘法器  \u_32x4乘法器_8  (.A(A[31:28]), .B(B), .Pl(\n32x4乘法器_8_pl ), .Ph(\n32x4乘法器_8_ph ));
  Shifter #(.width(32), .shift("ll")) shifter_1 (.in(\n32x4乘法器_2_pl ), .\dist (5'b00100), .out(shifter_1_out));
  Shifter #(.width(32), .shift("ll")) shifter_2 (.in(\n32x4乘法器_3_pl ), .\dist (5'b01000), .out(shifter_2_out));
  Shifter #(.width(32), .shift("ll")) shifter_3 (.in(\n32x4乘法器_4_pl ), .\dist (5'b01100), .out(shifter_3_out));
  Shifter #(.width(32), .shift("ll")) shifter_4 (.in(\n32x4乘法器_5_pl ), .\dist (5'b10000), .out(shifter_4_out));
  Shifter #(.width(32), .shift("ll")) shifter_5 (.in(\n32x4乘法器_6_pl ), .\dist (5'b10100), .out(shifter_5_out));
  Shifter #(.width(32), .shift("ll")) shifter_6 (.in(\n32x4乘法器_7_pl ), .\dist (5'b11000), .out(shifter_6_out));
  Shifter #(.width(32), .shift("ll")) shifter_7 (.in(\n32x4乘法器_8_pl ), .\dist (5'b11100), .out(shifter_7_out));
  Shifter #(.width(32), .shift("lr")) shifter_8 (.in(\n32x4乘法器_2_pl ), .\dist (5'b11100), .out(shifter_8_out));
  Adder #(.width(32)) adder_1 (
    .a(\n32x4乘法器_1_pl ), .b(shifter_1_out), .out(adder_1_out), .cout(adder_1_cout));  // open: cin
  Shifter #(.width(32), .shift("lr")) shifter_9 (.in(\n32x4乘法器_3_pl ), .\dist (5'b11000), .out(shifter_9_out));
  Adder #(.width(32)) adder_2 (
    .a(adder_1_out), .b(shifter_2_out), .out(adder_2_out), .cout(adder_2_cout));  // open: cin
  Shifter #(.width(32), .shift("lr")) shifter_10 (.in(\n32x4乘法器_4_pl ), .\dist (5'b10100), .out(shifter_10_out));
  Adder #(.width(32)) adder_3 (
    .a(adder_2_out), .b(shifter_3_out), .out(adder_3_out), .cout(adder_3_cout));  // open: cin
  Shifter #(.width(32), .shift("lr")) shifter_11 (.in(\n32x4乘法器_5_pl ), .\dist (5'b10000), .out(shifter_11_out));
  Adder #(.width(32)) adder_4 (
    .a(adder_3_out), .b(shifter_4_out), .out(adder_4_out), .cout(adder_4_cout));  // open: cin
  Shifter #(.width(32), .shift("lr")) shifter_12 (.in(\n32x4乘法器_6_pl ), .\dist (5'b01100), .out(shifter_12_out));
  Adder #(.width(32)) adder_5 (
    .a(adder_4_out), .b(shifter_5_out), .out(adder_5_out), .cout(adder_5_cout));  // open: cin
  Shifter #(.width(32), .shift("lr")) shifter_13 (.in(\n32x4乘法器_7_pl ), .\dist (5'b01000), .out(shifter_13_out));
  Adder #(.width(32)) adder_6 (
    .a(adder_5_out), .b(shifter_6_out), .out(adder_6_out), .cout(adder_6_cout));  // open: cin
  Shifter #(.width(32), .shift("lr")) shifter_14 (.in(\n32x4乘法器_8_pl ), .\dist (5'b00100), .out(shifter_14_out));
  Adder #(.width(32)) adder_7 (.a(adder_6_out), .b(shifter_7_out), .out(Pl), .cout(adder_7_cout));  // open: cin
  Adder #(.width(32)) adder_8 (
    .a(\n32x4乘法器_1_ph ), .b(shifter_15_out), .out(adder_8_out), .cin(adder_1_cout));  // open: cout
  Shifter #(.width(32), .shift("ll")) shifter_15 (.in(\n32x4乘法器_2_ph ), .\dist (5'b00100), .out(shifter_15_out));
  Adder #(.width(32)) adder_9 (
    .a(adder_8_out), .b(shifter_16_out), .out(adder_9_out), .cin(adder_2_cout));  // open: cout
  Shifter #(.width(32), .shift("ll")) shifter_16 (.in(\n32x4乘法器_3_ph ), .\dist (5'b01000), .out(shifter_16_out));
  Adder #(.width(32)) adder_10 (
    .a(adder_9_out), .b(shifter_17_out), .out(adder_10_out), .cin(adder_3_cout));  // open: cout
  Shifter #(.width(32), .shift("ll")) shifter_17 (.in(\n32x4乘法器_4_ph ), .\dist (5'b01100), .out(shifter_17_out));
  Adder #(.width(32)) adder_11 (
    .a(adder_10_out), .b(shifter_18_out), .out(adder_11_out), .cin(adder_4_cout));  // open: cout
  Shifter #(.width(32), .shift("ll")) shifter_18 (.in(\n32x4乘法器_5_ph ), .\dist (5'b10000), .out(shifter_18_out));
  Adder #(.width(32)) adder_12 (
    .a(adder_11_out), .b(shifter_19_out), .out(adder_12_out), .cin(adder_5_cout));  // open: cout
  Shifter #(.width(32), .shift("ll")) shifter_19 (.in(\n32x4乘法器_6_ph ), .\dist (5'b10100), .out(shifter_19_out));
  Adder #(.width(32)) adder_13 (
    .a(adder_12_out), .b(shifter_20_out), .out(adder_13_out), .cin(adder_6_cout));  // open: cout
  Shifter #(.width(32), .shift("ll")) shifter_20 (.in(\n32x4乘法器_7_ph ), .\dist (5'b11000), .out(shifter_20_out));
  Adder #(.width(32)) adder_14 (
    .a(adder_13_out), .b(shifter_21_out), .out(adder_14_out), .cin(adder_7_cout));  // open: cout
  Shifter #(.width(32), .shift("ll")) shifter_21 (.in(\n32x4乘法器_8_ph ), .\dist (5'b11100), .out(shifter_21_out));
  Adder #(.width(32)) adder_15 (.a(shifter_8_out), .b(shifter_9_out), .out(adder_15_out));  // open: cin, cout
  Adder #(.width(32)) adder_16 (.a(adder_15_out), .b(shifter_10_out), .out(adder_16_out));  // open: cin, cout
  Adder #(.width(32)) adder_17 (.a(adder_16_out), .b(shifter_11_out), .out(adder_17_out));  // open: cin, cout
  Adder #(.width(32)) adder_18 (.a(adder_17_out), .b(shifter_12_out), .out(adder_18_out));  // open: cin, cout
  Adder #(.width(32)) adder_19 (.a(adder_18_out), .b(shifter_13_out), .out(adder_19_out));  // open: cin, cout
  Adder #(.width(32)) adder_20 (.a(adder_19_out), .b(shifter_14_out), .out(adder_20_out));  // open: cin, cout
  Adder #(.width(32)) adder_21 (.a(adder_20_out), .b(adder_14_out), .out(Ph));  // open: cin, cout
endmodule

module \_32X32乘法器测试电路  (
  input  [31:0] in_1,
  input  [31:0] in_2,
  output [31:0] out_3,
  output [31:0] out_4,
  output [31:0] out_5,
  output [31:0] out_6
);

  \_32X32乘法器  \u_32x32乘法器_1  (.A(in_1), .B(in_2), .Pl(out_5), .Ph(out_3));
  Multiplier #(.width(32)) multiplier_1 (.a(in_1), .b(in_2), .out(out_6), .cout(out_4));  // open: cin
endmodule
