// Logisim project 实验4-CS1804-U201814755-彭子晨.circ as structural Verilog: 5 circuits, main circuit 四位除法器
module \四位除法器  (
  input  [3:0] n2,
  input  [3:0] d,
  output [3:0] quot,
  output [3:0] rem
);

  wire comparator_1_lt, comparator_2_lt, comparator_3_lt, comparator_4_lt, not_1_out, not_2_out, not_3_out,
       not_4_out, not_5_out, not_6_out, not_7_out, not_8_out;
  wire [0:0] multiplexer_1_out, multiplexer_3_out, multiplexer_5_out;
  wire [3:0] multiplexer_2_out, multiplexer_4_out, multiplexer_6_out, subtractor_1_out, subtractor_2_out,
       subtractor_3_out, subtractor_4_out;
  wire [7:0] shifter_1_out, shifter_2_out, shifter_3_out, shifter_4_out;

  Shifter #(.width(8), .shift("ll")) shifter_1 (.in({4'b0000, n2}), .\dist (3'b001), .out(shifter_1_out));
  Shifter #(.width(8), .shift("ll")) shifter_2 (
    .in({multiplexer_2_out, shifter_1_out[3:1], multiplexer_1_out[0]}), .\dist (3'b001), .out(shifter_2_out));
  Shifter #(.width(8), .shift("ll")) shifter_3 (
    .in({multiplexer_4_out, shifter_2_out[3:1], multiplexer_3_out[0]}), .\dist (3'b001), .out(shifter_3_out));
  Shifter #(.width(8), .shift("ll")) shifter_4 (
    .in({multiplexer_6_out, shifter_3_out[3:1], multiplexer_5_out[0]}), .\dist (3'b001),
    .out({shifter_4_out[7:4], quot[3:1], shifter_4_out[0]}));
  Multiplexer #(.select(1), .width(1), .disabled("Z"), .enable("false")) multiplexer_1 (
    .in0(shifter_1_out[0]), .in1(not_1_out), .out(multiplexer_1_out[0]), .sel(not_2_out));
  not not_1 (not_1_out, shifter_1_out[0]);
  Comparator #(.width(4), .mode("unsigned")) comparator_1 (
    .a(shifter_1_out[7:4]), .b(d), .lt(comparator_1_lt));  // open: gt, eq
  not not_2 (not_2_out, comparator_1_lt);
  Multiplexer #(.select(1), .width(4), .disabled("Z"), .enable("false")) multiplexer_2 (
    .in0(shifter_1_out[7:4]), .in1(subtractor_1_out), .out(multiplexer_2_out), .sel(not_2_out));
  Subtractor #(.width(4)) subtractor_1 (.a(shifter_1_out[7:4]), .b(d), .out(subtractor_1_out));  // open: bin, bout
  Multiplexer #(.select(1), .width(1), .disabled("Z"), .enable("false")) multiplexer_3 (
    .in0(shifter_2_out[0]), .in1(not_3_out), .out(multiplexer_3_out[0]), .sel(not_4_out));
  not not_3 (not_3_out, shifter_2_out[0]);
  Comparator #(.width(4), .mode("unsigned")) comparator_2 (
    .a(shifter_2_out[7:4]), .b(d), .lt(comparator_2_lt));  // open: gt, eq
  not not_4 (not_4_out, comparator_2_lt);
  Multiplexer #(.select(1), .width(4), .disabled("Z"), .enable("false")) multiplexer_4 (
    .in0(shifter_2_out[7:4]), .in1(subtractor_2_out), .out(multiplexer_4_out), .sel(not_4_out));
  Subtractor #(.width(4)) subtractor_2 (.a(shifter_2_out[7:4]), .b(d), .out(subtractor_2_out));  // open: bin, bout
  Multiplexer #(.select(1), .width(1), .disabled("Z"), .enable("false")) multiplexer_5 (
    .in0(shifter_3_out[0]), .in1(not_5_out), .out(multiplexer_5_out[0]), .sel(not_6_out));
  not not_5 (not_5_out, shifter_3_out[0]);
  Comparator #(.width(4), .mode("unsigned")) comparator_3 (
    .a(shifter_3_out[7:4]), .b(d), .lt(comparator_3_lt));  // open: gt, eq
  not not_6 (not_6_out, comparator_3_lt);
  Multiplexer #(.select(1), .width(4), .disabled("Z"), .enable("false")) multiplexer_6 (
    .in0(shifter_3_out[7:4]), .in1(subtractor_3_out), .out(multiplexer_6_out), .sel(not_6_out));
  Subtractor #(.width(4)) subtractor_3 (.a(shifter_3_out[7:4]), .b(d), .out(subtractor_3_out));  // open: bin, bout
  Multiplexer #(.select(1), .width(1), .disabled("Z"), .enable("false")) multiplexer_7 (
    .in0(shifter_4_out[0]), .in1(not_7_out), .out(quot[0]), .sel(not_8_out));
  not not_7 (not_7_out, shifter_4_out[0]);
  Comparator #(.width(4), .mode("unsigned")) comparator_4 (
    .a(shifter_4_out[7:4]), .b(d), .lt(comparator_4_lt));  // open: gt, eq
  not not_8 (not_8_out, comparator_4_lt);
  Multiplexer #(.select(1), .width(4), .disabled("Z"), .enable("false")) multiplexer_8 (
    .in0(shifter_4_out[7:4]), .in1(subtractor_4_out), .out(rem), .sel(not_8_out));
  Subtractor #(.width(4)) subtractor_4 (.a(shifter_4_out[7:4]), .b(d), .out(subtractor_4_out));  // open: bin, bout
  // Probe on {multiplexer_2_out, shifter_1_out[3:1], multiplexer_1_out[0]}

  // Notes on the sheet:
  //   n1
endmodule

module \四位除法器测试电路  (
  input  [3:0] in_1,
  input  [3:0] in_2,
  output [3:0] quot,
  output [3:0] rem
);

  \四位除法器  \u_四位除法器_1  (.n2(in_1), .d(in_2), .quot(quot), .rem(rem));
endmodule

module Div1 (
  input  [31:0] d,
  input  [31:0] cur_rem,
  input  [31:0] cur_quot,
  output [31:0] rem,
  output [31:0] quot
);

  wire comparator_1_eq, comparator_1_gt, or_1_out;
  wire [31:0] adder_1_out, adder_2_out, shifter_1_out, shifter_2_out, shifter_3_out, subtractor_1_out;

  Shifter #(.width(32), .shift("ll")) shifter_1 (.in(cur_rem), .\dist (5'b00001), .out(shifter_1_out));
  Shifter #(.width(32), .shift("lr")) shifter_2 (.in(cur_quot), .\dist ({5{1'b1}}), .out(shifter_2_out));
  Shifter #(.width(32), .shift("ll")) shifter_3 (.in(cur_quot), .\dist (5'b00001), .out(shifter_3_out));
  Adder #(.width(32)) adder_1 (.a(shifter_1_out), .b(shifter_2_out), .out(adder_1_out));  // open: cin, cout
  Adder #(.width(32)) adder_2 (.a(shifter_3_out), .b(32'h1), .out(adder_2_out));  // open: cin, cout
  Comparator #(.width(32), .mode("unsigned")) comparator_1 (
    .a(adder_1_out), .b(d), .gt(comparator_1_gt), .eq(comparator_1_eq));  // open: lt
  Subtractor #(.width(32)) subtractor_1 (.a(adder_1_out), .b(d), .out(subtractor_1_out));  // open: bin, bout
  or or_1 (or_1_out, comparator_1_gt, comparator_1_eq);
  Multiplexer #(.select(1), .width(32), .disabled("Z"), .enable("false")) multiplexer_1 (
    .in0(adder_1_out), .in1(subtractor_1_out), .out(rem), .sel(or_1_out));
  Multiplexer #(.select(1), .width(32), .disabled("Z"), .enable("false")) multiplexer_2 (
    .in0(shifter_3_out), .in1(adder_2_out), .out(quot), .sel(or_1_out));
endmodule

module \_32位除法器  (
  input  [31:0] d,
  input  [31:0] n,
  output [31:0] rem,
  output [31:0] quot
);

  wire comparator_1_eq;
  wire [31:0] div1_1_quot, div1_1_rem, div1_2_quot, div1_3_quot, div1_3_rem, div1_4_quot, div1_4_rem,
       div1_5_quot, div1_5_rem, div1_6_quot, div1_6_rem, div1_7_quot, div1_7_rem, div1_8_quot, div1_8_rem,
       div1_9_quot, div1_9_rem, div1_10_quot, div1_10_rem, div1_11_quot, div1_11_rem, div1_12_quot,
       div1_12_rem, div1_13_quot, div1_13_rem, div1_14_quot, div1_14_rem, div1_15_quot, div1_15_rem,
       div1_16_quot, div1_16_rem, div1_17_quot, div1_17_rem, div1_18_quot, div1_18_rem, div1_19_quot,
       div1_19_rem, div1_20_quot, div1_20_rem, div1_21_quot, div1_21_rem, div1_22_quot, div1_22_rem,
       div1_23_quot, div1_23_rem, div1_24_quot, div1_24_rem, div1_25_quot, div1_25_rem, div1_26_quot,
       div1_26_rem, div1_27_quot, div1_27_rem, div1_28_quot, div1_28_rem, div1_29_quot, div1_29_rem,
       div1_30_quot, div1_30_rem, div1_31_quot, div1_31_rem, div1_32_quot, div1_32_rem;

  Div1 div1_1 (.d(d), .cur_rem(div1_4_rem), .cur_quot(div1_4_quot), .rem(div1_1_rem), .quot(div1_1_quot));
  Div1 div1_2 (.d(d), .cur_rem(div1_6_rem), .cur_quot(div1_6_quot), .rem(rem), .quot(div1_2_quot));
  Comparator #(.width(32), .mode("twosComplement")) comparator_1 (
    .a(d), .b({32{1'b0}}), .eq(comparator_1_eq));  // open: gt, lt
  Multiplexer #(.select(1), .width(32), .disabled("Z"), .enable("false")) multiplexer_1 (
    .in0(div1_2_quot), .in1({32{1'b0}}), .out(quot), .sel(comparator_1_eq));
  Div1 div1_3 (.d(d), .cur_rem({32{1'b0}}), .cur_quot(n), .rem(div1_3_rem), .quot(div1_3_quot));
  Div1 div1_4 (.d(d), .cur_rem(div1_8_rem), .cur_quot(div1_8_quot), .rem(div1_4_rem), .quot(div1_4_quot));
  Div1 div1_5 (.d(d), .cur_rem(div1_1_rem), .cur_quot(div1_1_quot), .rem(div1_5_rem), .quot(div1_5_quot));
  Div1 div1_6 (.d(d), .cur_rem(div1_10_rem), .cur_quot(div1_10_quot), .rem(div1_6_rem), .quot(div1_6_quot));
  Div1 div1_7 (.d(d), .cur_rem(div1_3_rem), .cur_quot(div1_3_quot), .rem(div1_7_rem), .quot(div1_7_quot));
  Div1 div1_8 (.d(d), .cur_rem(div1_12_rem), .cur_quot(div1_12_quot), .rem(div1_8_rem), .quot(div1_8_quot));
  Div1 div1_9 (.d(d), .cur_rem(div1_5_rem), .cur_quot(div1_5_quot), .rem(div1_9_rem), .quot(div1_9_quot));
  Div1 div1_10 (.d(d), .cur_rem(div1_14_rem), .cur_quot(div1_14_quot), .rem(div1_10_rem), .quot(div1_10_quot));
  Div1 div1_11 (.d(d), .cur_rem(div1_7_rem), .cur_quot(div1_7_quot), .rem(div1_11_rem), .quot(div1_11_quot));
  Div1 div1_12 (.d(d), .cur_rem(div1_16_rem), .cur_quot(div1_16_quot), .rem(div1_12_rem), .quot(div1_12_quot));
  Div1 div1_13 (.d(d), .cur_rem(div1_9_rem), .cur_quot(div1_9_quot), .rem(div1_13_rem), .quot(div1_13_quot));
  Div1 div1_14 (.d(d), .cur_rem(div1_18_rem), .cur_quot(div1_18_quot), .rem(div1_14_rem), .quot(div1_14_quot));
  Div1 div1_15 (.d(d), .cur_rem(div1_11_rem), .cur_quot(div1_11_quot), .rem(div1_15_rem), .quot(div1_15_quot));
  Div1 div1_16 (.d(d), .cur_rem(div1_20_rem), .cur_quot(div1_20_quot), .rem(div1_16_rem), .quot(div1_16_quot));
  Div1 div1_17 (.d(d), .cur_rem(div1_13_rem), .cur_quot(div1_13_quot), .rem(div1_17_rem), .quot(div1_17_quot));
  Div1 div1_18 (.d(d), .cur_rem(div1_22_rem), .cur_quot(div1_22_quot), .rem(div1_18_rem), .quot(div1_18_quot));
  Div1 div1_19 (.d(d), .cur_rem(div1_15_rem), .cur_quot(div1_15_quot), .rem(div1_19_rem), .quot(div1_19_quot));
  Div1 div1_20 (.d(d), .cur_rem(div1_24_rem), .cur_quot(div1_24_quot), .rem(div1_20_rem), .quot(div1_20_quot));
  Div1 div1_21 (.d(d), .cur_rem(div1_17_rem), .cur_quot(div1_17_quot), .rem(div1_21_rem), .quot(div1_21_quot));
  Div1 div1_22 (.d(d), .cur_rem(div1_26_rem), .cur_quot(div1_26_quot), .rem(div1_22_rem), .quot(div1_22_quot));
  Div1 div1_23 (.d(d), .cur_rem(div1_19_rem), .cur_quot(div1_19_quot), .rem(div1_23_rem), .quot(div1_23_quot));
  Div1 div1_24 (.d(d), .cur_rem(div1_28_rem), .cur_quot(div1_28_quot), .rem(div1_24_rem), .quot(div1_24_quot));
  Div1 div1_25 (.d(d), .cur_rem(div1_21_rem), .cur_quot(div1_21_quot), .rem(div1_25_rem), .quot(div1_25_quot));
  Div1 div1_26 (.d(d), .cur_rem(div1_30_rem), .cur_quot(div1_30_quot), .rem(div1_26_rem), .quot(div1_26_quot));
  Div1 div1_27 (.d(d), .cur_rem(div1_23_rem), .cur_quot(div1_23_quot), .rem(div1_27_rem), .quot(div1_27_quot));
  Div1 div1_28 (.d(d), .cur_rem(div1_31_rem), .cur_quot(div1_31_quot), .rem(div1_28_rem), .quot(div1_28_quot));
  Div1 div1_29 (.d(d), .cur_rem(div1_25_rem), .cur_quot(div1_25_quot), .rem(div1_29_rem), .quot(div1_29_quot));
  Div1 div1_30 (.d(d), .cur_rem(div1_32_rem), .cur_quot(div1_32_quot), .rem(div1_30_rem), .quot(div1_30_quot));
  Div1 div1_31 (.d(d), .cur_rem(div1_27_rem), .cur_quot(div1_27_quot), .rem(div1_31_rem), .quot(div1_31_quot));
  Div1 div1_32 (.d(d), .cur_rem(div1_29_rem), .cur_quot(div1_29_quot), .rem(div1_32_rem), .quot(div1_32_quot));
endmodule

module \_32位除法器测试电路  (
  input  [31:0] in_1,
  input  [31:0] in_2,
  output [31:0] out_3,
  output [31:0] out_4,
  output [31:0] out_5,
  output [31:0] out_6
);

  Divider #(.width(32)) divider_1 (.a(in_1), .b(in_2), .out(out_4), .rem(out_6));  // open: upper
  \_32位除法器  \u_32位除法器_1  (.d(in_2), .n(in_1), .quot(out_3), .rem(out_5));
endmodule
