// Logisim project 实验5-CS1804-U201814755-彭子晨.circ as structural Verilog: 14 circuits, main circuit 秒脉冲产生电路
module \四位二进制可逆计数器  (
  input  CLR,
  input  nDL,
  input  CPu,
  input  CPd,
  input  A,
  input  B,
  input  C,
  input  D,
  output Qa,
  output Qb,
  output Qc,
  output Qd
);

  wire and_1_out, and_2_out, and_3_out, and_4_out, and_5_out, and_6_out, and_7_out, and_8_out, and_9_out,
       and_10_out, and_11_out, and_12_out, and_13_out, and_14_out, d_ff_1_qn, d_ff_2_qn, d_ff_3_qn,
       d_ff_4_qn, not_1_out, not_2_out, not_3_out, not_4_out, not_5_out, not_6_out, not_7_out, not_8_out,
       not_9_out, not_10_out, not_11_out, or_1_out, or_2_out, or_3_out, or_4_out, or_5_out, or_6_out,
       or_7_out, or_8_out;

  not not_1 (not_1_out, Qa);
  not not_2 (not_2_out, Qa);
  not not_3 (not_3_out, Qb);
  not not_4 (not_4_out, Qa);
  not not_5 (not_5_out, Qb);
  not not_6 (not_6_out, Qc);
  or or_1 (or_1_out, CPu, CPd);
  and and_1 (and_1_out, CPu, Qa);
  and and_2 (and_2_out, CPd, not_1_out);
  and and_3 (and_3_out, CPu, Qa, Qb);
  or or_2 (or_2_out, and_3_out, and_4_out);
  and and_4 (and_4_out, CPd, not_2_out, not_3_out);
  and and_5 (and_5_out, CPu, Qa, Qb, Qc);
  or or_3 (or_3_out, and_5_out, and_6_out);
  and and_6 (and_6_out, CPd, not_4_out, not_5_out, not_6_out);
  D_Flip_Flop #(.trigger("falling"), .Pre_Clr_Positions("LEGACY"), .NegatePresetClear("false"), .enable("true"), .NewFFLayout("false")) d_ff_1 (
    .clk(or_1_out), .D(d_ff_1_qn), .Q(Qa), .Qn(d_ff_1_qn), .preset(and_7_out), .reset(or_4_out));  // open: en
  or or_4 (or_4_out, CLR, and_8_out);
  D_Flip_Flop #(.trigger("falling"), .Pre_Clr_Positions("LEGACY"), .NegatePresetClear("false"), .enable("true"), .NewFFLayout("false")) d_ff_2 (
    .clk(or_5_out), .D(d_ff_2_qn), .Q(Qb), .Qn(d_ff_2_qn), .preset(and_9_out), .reset(or_6_out));  // open: en
  or or_5 (or_5_out, and_1_out, and_2_out);
  or or_6 (or_6_out, CLR, and_10_out);
  D_Flip_Flop #(.trigger("falling"), .Pre_Clr_Positions("LEGACY"), .NegatePresetClear("false"), .enable("true"), .NewFFLayout("false")) d_ff_3 (
    .clk(or_2_out), .D(d_ff_3_qn), .Q(Qc), .Qn(d_ff_3_qn), .preset(and_11_out), .reset(or_7_out));  // open: en
  or or_7 (or_7_out, CLR, and_12_out);
  D_Flip_Flop #(.trigger("falling"), .Pre_Clr_Positions("LEGACY"), .NegatePresetClear("false"), .enable("true"), .NewFFLayout("false")) d_ff_4 (
    .clk(or_3_out), .D(d_ff_4_qn), .Q(Qd), .Qn(d_ff_4_qn), .preset(and_13_out), .reset(or_8_out));  // open: en
  or or_8 (or_8_out, CLR, and_14_out);
  not not_7 (not_7_out, nDL);
  and and_7 (and_7_out, A, not_7_out);
  and and_8 (and_8_out, not_8_out, not_7_out);
  and and_9 (and_9_out, B, not_7_out);
  and and_10 (and_10_out, not_9_out, not_7_out);
  and and_11 (and_11_out, C, not_7_out);
  and and_12 (and_12_out, not_10_out, not_7_out);
  and and_13 (and_13_out, D, not_7_out);
  and and_14 (and_14_out, not_11_out, not_7_out);
  not not_8 (not_8_out, A);
  not not_9 (not_9_out, B);
  not not_10 (not_10_out, C);
  not not_11 (not_11_out, D);
endmodule

module \六十进制计数器  (
  input  CPu,
  input  Clr,
  input  CPd,
  input  Adj,
  output Q1D,
  output Q1C,
  output Q1B,
  output Q1A,
  output Q0D,
  output Q0C,
  output Q0B,
  output Q0A,
  output nQCC
);

  wire and_1_out, and_2_out, and_3_out, and_4_out, and_5_out, and_6_out, nor_1_out, nor_2_out, not_1_out,
       not_2_out, or_1_out;
  wire [3:0] \四位二进制可逆计数器_1_qa , \四位二进制可逆计数器_2_qa ;
  wire [5:0] adder_1_out, multiplier_1_out;
  wire [5:4] divider_1_out, divider_1_rem;

  and and_1 (and_1_out, \四位二进制可逆计数器_1_qa [1], \四位二进制可逆计数器_1_qa [0], \四位二进制可逆计数器_2_qa [3], \四位二进制可逆计数器_2_qa [2]);
  not not_1 (not_1_out, and_2_out);
  and and_2 (and_2_out, nor_1_out, nor_2_out);
  and and_3 (and_3_out, CPu, and_5_out);
  nor nor_1 (nor_1_out, \四位二进制可逆计数器_1_qa [3], \四位二进制可逆计数器_1_qa [2], \四位二进制可逆计数器_1_qa [1], \四位二进制可逆计数器_1_qa [0]);
  and and_4 (and_4_out, CPd, not_1_out, nor_2_out);
  not not_2 (not_2_out, Adj);
  nor nor_2 (nor_2_out, \四位二进制可逆计数器_2_qa [0], \四位二进制可逆计数器_2_qa [1], \四位二进制可逆计数器_2_qa [2], \四位二进制可逆计数器_2_qa [3]);
  and and_5 (and_5_out, \四位二进制可逆计数器_2_qa [3], \四位二进制可逆计数器_2_qa [2], \四位二进制可逆计数器_2_qa [1], \四位二进制可逆计数器_2_qa [0]);
  or or_1 (or_1_out, and_1_out, Clr);
  and and_6 (and_6_out, CPd, not_1_out, Adj);
  and and_7 (nQCC, not_2_out, and_1_out);
  \四位二进制可逆计数器  \u_四位二进制可逆计数器_1  (
    .CPu(and_3_out), .CPd(and_4_out), .Qa(\四位二进制可逆计数器_1_qa [0]), .A(1'b0), .Qb(\四位二进制可逆计数器_1_qa [1]),
    .B(1'b0), .Qc(\四位二进制可逆计数器_1_qa [2]), .C(1'b0), .Qd(\四位二进制可逆计数器_1_qa [3]), .D(1'b0), .CLR(and_1_out),
    .nDL(1'b1));
  \四位二进制可逆计数器  \u_四位二进制可逆计数器_2  (
    .CPu(CPu), .CPd(and_6_out), .Qa(\四位二进制可逆计数器_2_qa [0]), .A(1'b0), .Qb(\四位二进制可逆计数器_2_qa [1]), .B(1'b0),
    .Qc(\四位二进制可逆计数器_2_qa [2]), .C(1'b0), .Qd(\四位二进制可逆计数器_2_qa [3]), .D(1'b0), .CLR(or_1_out), .nDL(1'b1));
  Multiplier #(.width(6)) multiplier_1 (
    .a({2'b00, \四位二进制可逆计数器_1_qa }), .b(6'b010000), .out(multiplier_1_out));  // open: cin, cout
  Adder #(.width(6)) adder_1 (
    .a(multiplier_1_out), .b({2'b00, \四位二进制可逆计数器_2_qa }), .out(adder_1_out));  // open: cin, cout
  Divider #(.width(6)) divider_1 (
    .a(adder_1_out), .b(6'b001010), .out({divider_1_out, Q1D, Q1C, Q1B, Q1A}),
    .rem({divider_1_rem, Q0D, Q0C, Q0B, Q0A}));  // open: upper
endmodule

module \六十进制计数器测试电路  (
  input  in_1,
  input  in_2,
  output out_3
);

  wire button_1_out, button_2_out;
  wire [3:0] \六十进制计数器_1_q0a , \六十进制计数器_1_q1a ;

  Button button_1 (.out(button_1_out));
  Button button_2 (.out(button_2_out));
  Hex_Digit_Display hex_digit_display_1 (.value(\六十进制计数器_1_q1a ));  // open: dp
  Hex_Digit_Display hex_digit_display_2 (.value(\六十进制计数器_1_q0a ));  // open: dp
  \六十进制计数器  \u_六十进制计数器_1  (
    .Q1D(\六十进制计数器_1_q1a [3]), .Q1C(\六十进制计数器_1_q1a [2]), .Q1B(\六十进制计数器_1_q1a [1]), .Q1A(\六十进制计数器_1_q1a [0]),
    .Q0D(\六十进制计数器_1_q0a [3]), .Q0C(\六十进制计数器_1_q0a [2]), .Q0B(\六十进制计数器_1_q0a [1]), .Q0A(\六十进制计数器_1_q0a [0]),
    .CPu(button_1_out), .Clr(in_2), .CPd(button_2_out), .Adj(in_1), .nQCC(out_3));
endmodule

module \十二进制计数器或二十四进制的计数器电路  (
  input  CPu,
  input  Clr,
  input  CPd,
  input  Adj,
  input  Set,
  output Q1D,
  output Q1C,
  output Q1B,
  output Q1A,
  output Q0D,
  output Q0C,
  output Q0B,
  output Q0A,
  output nQCC
);

  wire and_1_out, and_2_out, and_4_out, and_5_out, and_6_out, and_7_out, comparator_1_eq, nor_1_out,
       nor_2_out, not_1_out, not_2_out, or_1_out, t_ff_1_q;
  wire [3:0] \四位二进制可逆计数器_1_qa , \四位二进制可逆计数器_2_qa ;
  wire [5:0] adder_1_out, adder_2_out, bit_extender_1_out, multiplexer_1_out, multiplexer_2_out,
       multiplexer_3_out, multiplier_1_out, multiplier_2_out;
  wire [5:4] divider_1_out, divider_1_rem;

  not not_1 (not_1_out, and_1_out);
  and and_1 (and_1_out, nor_1_out, nor_2_out);
  and and_2 (and_2_out, CPu, and_5_out);
  and and_3 (nQCC, \四位二进制可逆计数器_2_qa [3], \四位二进制可逆计数器_2_qa [2]);
  nor nor_1 (nor_1_out, \四位二进制可逆计数器_1_qa [3], \四位二进制可逆计数器_1_qa [2], \四位二进制可逆计数器_1_qa [1], \四位二进制可逆计数器_1_qa [0]);
  and and_4 (and_4_out, CPd, not_1_out, nor_2_out);
  nor nor_2 (nor_2_out, \四位二进制可逆计数器_2_qa [0], \四位二进制可逆计数器_2_qa [1], \四位二进制可逆计数器_2_qa [2], \四位二进制可逆计数器_2_qa [3]);
  and and_5 (and_5_out, \四位二进制可逆计数器_2_qa [3], \四位二进制可逆计数器_2_qa [2], \四位二进制可逆计数器_2_qa [1], \四位二进制可逆计数器_2_qa [0]);
  or or_1 (or_1_out, nQCC, Clr);
  and and_6 (and_6_out, CPd, not_1_out, Adj);
  \四位二进制可逆计数器  \u_四位二进制可逆计数器_1  (
    .CPu(and_2_out), .CPd(and_4_out), .Qa(\四位二进制可逆计数器_1_qa [0]), .A(1'b0), .Qb(\四位二进制可逆计数器_1_qa [1]),
    .B(1'b0), .Qc(\四位二进制可逆计数器_1_qa [2]), .C(1'b0), .Qd(\四位二进制可逆计数器_1_qa [3]), .D(1'b0), .CLR(nQCC), .nDL(1'b1));
  \四位二进制可逆计数器  \u_四位二进制可逆计数器_2  (
    .CPu(CPu), .CPd(and_6_out), .Qa(\四位二进制可逆计数器_2_qa [0]), .A(1'b0), .Qb(\四位二进制可逆计数器_2_qa [1]), .B(1'b0),
    .Qc(\四位二进制可逆计数器_2_qa [2]), .C(1'b0), .Qd(\四位二进制可逆计数器_2_qa [3]), .D(1'b0), .CLR(or_1_out), .nDL(1'b1));
  T_Flip_Flop #(.trigger("rising"), .Pre_Clr_Positions("LEGACY"), .NegatePresetClear("false"), .enable("true"), .NewFFLayout("false")) t_ff_1 (
    .clk(nQCC), .T(1'b1), .Q(t_ff_1_q));  // open: Qn, preset, reset, en
  Multiplier #(.width(6)) multiplier_1 (
    .a({2'b00, \四位二进制可逆计数器_1_qa }), .b(6'b010000), .out(multiplier_1_out));  // open: cin, cout
  Adder #(.width(6)) adder_1 (
    .a(multiplier_1_out), .b({2'b00, \四位二进制可逆计数器_2_qa }), .out(adder_1_out));  // open: cin, cout
  assign bit_extender_1_out = {{5{1'b0}}, t_ff_1_q};  // Bit_Extender bit_extender_1
  Divider #(.width(6)) divider_1 (
    .a(multiplexer_2_out), .b(6'b001010), .out({divider_1_out, Q1D, Q1C, Q1B, Q1A}),
    .rem({divider_1_rem, Q0D, Q0C, Q0B, Q0A}));  // open: upper
  Multiplexer #(.select(1), .width(6), .disabled("Z"), .enable("false")) multiplexer_1 (
    .in0(adder_1_out), .in1(6'b001100), .out(multiplexer_1_out), .sel(comparator_1_eq));
  Comparator #(.width(6), .mode("unsigned")) comparator_1 (
    .a(adder_1_out), .b({6{1'b0}}), .eq(comparator_1_eq));  // open: gt, lt
  not not_2 (not_2_out, t_ff_1_q);
  Multiplier #(.width(6)) multiplier_2 (
    .a(bit_extender_1_out), .b(6'b001100), .out(multiplier_2_out));  // open: cin, cout
  and and_7 (and_7_out, comparator_1_eq, not_2_out);
  Adder #(.width(6)) adder_2 (.a(adder_1_out), .b(multiplier_2_out), .out(adder_2_out));  // open: cin, cout
  Multiplexer #(.select(1), .width(6), .disabled("Z"), .enable("false")) multiplexer_2 (
    .in0(multiplexer_1_out), .in1(multiplexer_3_out), .out(multiplexer_2_out), .sel(Set));
  Multiplexer #(.select(1), .width(6), .disabled("Z"), .enable("false")) multiplexer_3 (
    .in0(adder_2_out), .in1({6{1'b0}}), .out(multiplexer_3_out), .sel(and_7_out));
endmodule

module \十二进制计数器或二十四进制的计数器测试电路  (
  input  in_1,
  input  in_2,
  input  in_3,
  input  in_4,
  input  in_5,
  output out_6
);

  wire [3:0] \十二进制计数器或二十四进制的计数器电路_1_q0a , \十二进制计数器或二十四进制的计数器电路_1_q1a ;

  Hex_Digit_Display hex_digit_display_1 (.value(\十二进制计数器或二十四进制的计数器电路_1_q1a ));  // open: dp
  Hex_Digit_Display hex_digit_display_2 (.value(\十二进制计数器或二十四进制的计数器电路_1_q0a ));  // open: dp
  \十二进制计数器或二十四进制的计数器电路  \u_十二进制计数器或二十四进制的计数器电路_1  (
    .CPu(in_1), .Clr(in_5), .CPd(in_4), .Adj(in_2), .Q1D(\十二进制计数器或二十四进制的计数器电路_1_q1a [3]),
    .Q1C(\十二进制计数器或二十四进制的计数器电路_1_q1a [2]), .Q1B(\十二进制计数器或二十四进制的计数器电路_1_q1a [1]),
    .Q1A(\十二进制计数器或二十四进制的计数器电路_1_q1a [0]), .Q0D(\十二进制计数器或二十四进制的计数器电路_1_q0a [3]),
    .Q0C(\十二进制计数器或二十四进制的计数器电路_1_q0a [2]), .Q0B(\十二进制计数器或二十四进制的计数器电路_1_q0a [1]),
    .Q0A(\十二进制计数器或二十四进制的计数器电路_1_q0a [0]), .Set(in_3), .nQCC(out_6));
endmodule

module \上下午文字显示的电路  (
  input  AM_FM,
  input  TT,
  output [6:0] \列1 ,
  output [6:0] \列2 ,
  output [6:0] \列3 ,
  output [6:0] \列4 ,
  output [6:0] \列5 
);

  wire [6:0] multiplexer_1_out, multiplexer_2_out;

  Multiplexer #(.select(1), .width(7), .disabled("Z"), .enable("false")) multiplexer_1 (
    .in0(7'b0001001), .in1(7'b1001000), .out(multiplexer_1_out), .sel(AM_FM));
  Multiplexer #(.select(1), .width(7), .disabled("Z"), .enable("false")) multiplexer_2 (
    .in0(7'b0000001), .in1(7'b1000000), .out(multiplexer_2_out), .sel(AM_FM));
  Multiplexer #(.select(1), .width(7), .disabled("Z"), .enable("false")) multiplexer_3 (
    .in0({7{1'b0}}), .in1(multiplexer_1_out), .out(\列3 ), .sel(TT));
  Multiplexer #(.select(1), .width(7), .disabled("Z"), .enable("false")) multiplexer_4 (
    .in0({7{1'b0}}), .in1({7{1'b1}}), .out(\列2 ), .sel(TT));
  Multiplexer #(.select(1), .width(7), .disabled("Z"), .enable("false")) multiplexer_5 (
    .in0({7{1'b0}}), .in1(multiplexer_2_out), .out(\列1 ), .sel(TT));

  assign \列4  = \列3 ;
  assign \列5  = \列1 ;
endmodule

module \上下午文字显示测试电路  (
  input  in_1,
  input  in_2
);

  wire [6:0] \上下午文字显示的电路_1_列1 , \上下午文字显示的电路_1_列2 , \上下午文字显示的电路_1_列3 , \上下午文字显示的电路_1_列4 , \上下午文字显示的电路_1_列5 ;

  DotMatrix #(.inputtype("column"), .matrixcols(5), .matrixrows(7), .persist(0), .dotshape("square")) dotmatrix_1 (
    .col0(\上下午文字显示的电路_1_列1 ), .col1(\上下午文字显示的电路_1_列2 ), .col2(\上下午文字显示的电路_1_列3 ), .col3(\上下午文字显示的电路_1_列4 ),
    .col4(\上下午文字显示的电路_1_列5 ));
  \上下午文字显示的电路  \u_上下午文字显示的电路_1  (
    .\列1 (\上下午文字显示的电路_1_列1 ), .\列2 (\上下午文字显示的电路_1_列2 ), .\列3 (\上下午文字显示的电路_1_列3 ), .\列4 (\上下午文字显示的电路_1_列4 ),
    .\列5 (\上下午文字显示的电路_1_列5 ), .AM_FM(in_1), .TT(in_2));
endmodule

module \电子钟整点报时电路  (
  input  [3:0] Min1,
  input  [3:0] Min2,
  input  [3:0] Sec1,
  output out_4
);

  wire comparator_1_eq, comparator_2_eq, comparator_3_eq;

  Comparator #(.width(4), .mode("twosComplement")) comparator_1 (
    .a(4'b0101), .b(Min1), .eq(comparator_1_eq));  // open: gt, lt
  and and_1 (out_4, comparator_1_eq, comparator_2_eq, comparator_3_eq);
  Comparator #(.width(4), .mode("twosComplement")) comparator_2 (
    .a(4'b1001), .b(Min2), .eq(comparator_2_eq));  // open: gt, lt
  Comparator #(.width(4), .mode("twosComplement")) comparator_3 (
    .a(4'b0101), .b(Sec1), .eq(comparator_3_eq));  // open: gt, lt
endmodule

module \电子钟整点报时电路测试电路  (
  input  [3:0] Min1,
  input  [3:0] Min2,
  input  [3:0] Sec1
);

  wire \电子钟整点报时电路_1_out_4 ;

  LED #(.active("true")) led_1 (.in(\电子钟整点报时电路_1_out_4 ));
  \电子钟整点报时电路  \u_电子钟整点报时电路_1  (.out_4(\电子钟整点报时电路_1_out_4 ), .Min1(Min1), .Min2(Min2), .Sec1(Sec1));
endmodule

module \多功能数字钟  (
  input  Alarm_On_Off,
  input  Alarm_Set,
  input  CP,
  input  CPu,
  input  CPd,
  input  Set,
  input  Clr,
  input  Adj1,
  input  Adj0,
  output [3:0] hour1,
  output [3:0] hour2,
  output [3:0] min1,
  output [3:0] min2,
  output [3:0] sec1,
  output [3:0] sec2,
  output \闹钟 ,
  output [6:0] led1,
  output [6:0] led2,
  output [6:0] led3,
  output [6:0] led4,
  output [6:0] led5,
  output \定点报时 
);

  wire and_1_out, and_2_out, multiplexer_5_out, multiplexer_7_out, not_1_out, or_1_out, or_2_out, t_ff_1_q,
       t_ff_2_q, \六十进制计数器_1_nqcc , \六十进制计数器_2_nqcc , \十二进制计数器或二十四进制的计数器电路_1_nqcc , \秒脉冲产生电路_1_out_2 ,
       \闹钟_1_nqcc ;
  wire [1:0] multiplexer_1_out, multiplexer_2_out;
  wire [3:0] \六十进制计数器_1_q0a , \六十进制计数器_1_q1a , \六十进制计数器_2_q0a , \六十进制计数器_2_q1a , \十二进制计数器或二十四进制的计数器电路_1_q0a ,
       \十二进制计数器或二十四进制的计数器电路_1_q1a , \闹钟_1_out_16 , \闹钟_1_out_20 , \闹钟_1_out_24 , \闹钟_1_out_28 ;

  Multiplexer #(.select(1), .width(2), .disabled("Z"), .enable("false")) multiplexer_1 (
    .in0(2'b01), .in1(2'b10), .out(multiplexer_1_out), .sel(Adj1));
  \闹钟  \u_闹钟_1  (
    .Alarm_Set(Alarm_Set), .Set(Set), .CPU(CPu), .Adj1(multiplexer_1_out[1]), .out_13(\闹钟_1_out_16 [3]),
    .out_14(\闹钟_1_out_16 [2]), .out_15(\闹钟_1_out_16 [1]), .out_16(\闹钟_1_out_16 [0]),
    .out_17(\闹钟_1_out_20 [3]), .out_18(\闹钟_1_out_20 [2]), .out_19(\闹钟_1_out_20 [1]),
    .out_20(\闹钟_1_out_20 [0]), .out_21(\闹钟_1_out_24 [3]), .out_22(\闹钟_1_out_24 [2]),
    .out_23(\闹钟_1_out_24 [1]), .out_24(\闹钟_1_out_24 [0]), .out_25(\闹钟_1_out_28 [3]),
    .out_26(\闹钟_1_out_28 [2]), .out_27(\闹钟_1_out_28 [1]), .out_28(\闹钟_1_out_28 [0]), .On_Off(Alarm_On_Off),
    .Alarm_out(\闹钟 ), .CPD(CPd), .Hour1(\十二进制计数器或二十四进制的计数器电路_1_q1a ), .Hour2(\十二进制计数器或二十四进制的计数器电路_1_q0a ),
    .Min1(\六十进制计数器_1_q1a ), .Min2(\六十进制计数器_1_q0a ), .Sec1(\六十进制计数器_2_q1a ), .nQcc(\闹钟_1_nqcc ));
  or or_1 (or_1_out, and_1_out, \六十进制计数器_1_nqcc );
  and and_1 (and_1_out, CPu, multiplexer_2_out[0]);
  Multiplexer #(.select(1), .width(2), .disabled("Z"), .enable("false")) multiplexer_2 (
    .in0(2'b00), .in1(multiplexer_1_out), .out(multiplexer_2_out), .sel(Adj0));
  Multiplexer #(.select(1), .width(4), .disabled("Z"), .enable("false")) multiplexer_3 (
    .in0(\十二进制计数器或二十四进制的计数器电路_1_q1a ), .in1(\闹钟_1_out_16 ), .out(hour1), .sel(Alarm_Set));
  Multiplexer #(.select(1), .width(4), .disabled("Z"), .enable("false")) multiplexer_4 (
    .in0(\十二进制计数器或二十四进制的计数器电路_1_q0a ), .in1(\闹钟_1_out_20 ), .out(hour2), .sel(Alarm_Set));
  \十二进制计数器或二十四进制的计数器电路  \u_十二进制计数器或二十四进制的计数器电路_1  (
    .CPu(or_1_out), .Clr(Clr), .CPd(CPd), .Adj(multiplexer_2_out[0]), .Q1D(\十二进制计数器或二十四进制的计数器电路_1_q1a [3]),
    .Q1C(\十二进制计数器或二十四进制的计数器电路_1_q1a [2]), .Q1B(\十二进制计数器或二十四进制的计数器电路_1_q1a [1]),
    .Q1A(\十二进制计数器或二十四进制的计数器电路_1_q1a [0]), .Q0D(\十二进制计数器或二十四进制的计数器电路_1_q0a [3]),
    .Q0C(\十二进制计数器或二十四进制的计数器电路_1_q0a [2]), .Q0B(\十二进制计数器或二十四进制的计数器电路_1_q0a [1]),
    .Q0A(\十二进制计数器或二十四进制的计数器电路_1_q0a [0]), .Set(Set), .nQCC(\十二进制计数器或二十四进制的计数器电路_1_nqcc ));
  not not_1 (not_1_out, Set);
  T_Flip_Flop #(.trigger("falling"), .Pre_Clr_Positions("LEGACY"), .NegatePresetClear("false"), .enable("true"), .NewFFLayout("false")) t_ff_1 (
    .clk(\闹钟_1_nqcc ), .T(1'b1), .Q(t_ff_1_q));  // open: Qn, preset, reset, en
  T_Flip_Flop #(.trigger("falling"), .Pre_Clr_Positions("LEGACY"), .NegatePresetClear("false"), .enable("true"), .NewFFLayout("false")) t_ff_2 (
    .clk(\十二进制计数器或二十四进制的计数器电路_1_nqcc ), .T(1'b1), .Q(t_ff_2_q));  // open: Qn, preset, reset, en
  or or_2 (or_2_out, and_2_out, \六十进制计数器_2_nqcc );
  and and_2 (and_2_out, CPu, multiplexer_2_out[1]);
  \上下午文字显示的电路  \u_上下午文字显示的电路_1  (
    .\列1 (led1), .\列2 (led2), .\列3 (led3), .\列4 (led4), .\列5 (led5), .AM_FM(multiplexer_5_out), .TT(not_1_out));
  Multiplexer #(.select(1), .width(1), .disabled("Z"), .enable("false")) multiplexer_5 (
    .in0(t_ff_2_q), .in1(t_ff_1_q), .out(multiplexer_5_out), .sel(Alarm_Set));
  Multiplexer #(.select(1), .width(4), .disabled("Z"), .enable("false")) multiplexer_6 (
    .in0(\六十进制计数器_1_q1a ), .in1(\闹钟_1_out_24 ), .out(min1), .sel(Alarm_Set));
  Multiplexer #(.select(1), .width(1), .disabled("Z"), .enable("false")) multiplexer_7 (
    .in0(CP), .in1(1'b0), .out(multiplexer_7_out), .sel(Adj0));
  Multiplexer #(.select(1), .width(4), .disabled("Z"), .enable("false")) multiplexer_8 (
    .in0(\六十进制计数器_1_q0a ), .in1(\闹钟_1_out_28 ), .out(min2), .sel(Alarm_Set));
  \六十进制计数器  \u_六十进制计数器_1  (
    .Q1D(\六十进制计数器_1_q1a [3]), .Q1C(\六十进制计数器_1_q1a [2]), .Q1B(\六十进制计数器_1_q1a [1]), .Q1A(\六十进制计数器_1_q1a [0]),
    .Q0D(\六十进制计数器_1_q0a [3]), .Q0C(\六十进制计数器_1_q0a [2]), .Q0B(\六十进制计数器_1_q0a [1]), .Q0A(\六十进制计数器_1_q0a [0]),
    .CPu(or_2_out), .Clr(Clr), .CPd(CPd), .Adj(multiplexer_2_out[1]), .nQCC(\六十进制计数器_1_nqcc ));
  \电子钟整点报时电路  \u_电子钟整点报时电路_1  (.out_4(\定点报时 ), .Min1(\六十进制计数器_1_q1a ), .Min2(\六十进制计数器_1_q0a ), .Sec1(\六十进制计数器_2_q1a ));
  \秒脉冲产生电路  \u_秒脉冲产生电路_1  (.out_2(\秒脉冲产生电路_1_out_2 ), .in_1(multiplexer_7_out));
  Multiplexer #(.select(1), .width(4), .disabled("Z"), .enable("false")) multiplexer_9 (
    .in0(\六十进制计数器_2_q1a ), .in1(4'b0000), .out(sec1), .sel(Alarm_Set));
  \六十进制计数器  \u_六十进制计数器_2  (
    .Q1D(\六十进制计数器_2_q1a [3]), .Q1C(\六十进制计数器_2_q1a [2]), .Q1B(\六十进制计数器_2_q1a [1]), .Q1A(\六十进制计数器_2_q1a [0]),
    .Q0D(\六十进制计数器_2_q0a [3]), .Q0C(\六十进制计数器_2_q0a [2]), .Q0B(\六十进制计数器_2_q0a [1]), .Q0A(\六十进制计数器_2_q0a [0]),
    .CPu(\秒脉冲产生电路_1_out_2 ), .Clr(Clr), .CPd(1'b0), .Adj(1'b0), .nQCC(\六十进制计数器_2_nqcc ));
  Multiplexer #(.select(1), .width(4), .disabled("Z"), .enable("false")) multiplexer_10 (
    .in0(\六十进制计数器_2_q0a ), .in1(4'b0000), .out(sec2), .sel(Alarm_Set));
endmodule

module \秒脉冲产生电路  (
  input  in_1,
  output out_2
);

  Counter #(.width(2), .max('h3), .ongoal("wrap"), .trigger("rising"), .behavior("old")) counter_1 (
    .D(2'b01), .count(1'b1), .carry(out_2), .clk(in_1));  // open: load, Q, clr, preset
endmodule

module \多功能数字钟测试电路  (
  input  in_1,
  input  in_2,
  input  in_3,
  input  in_4,
  input  in_5,
  input  in_6
);

  wire button_1_out, button_2_out, clock_1_out, \多功能数字钟_1_定点报时 , \多功能数字钟_1_闹钟 ;
  wire [3:0] \多功能数字钟_1_hour1 , \多功能数字钟_1_hour2 , \多功能数字钟_1_min1 , \多功能数字钟_1_min2 , \多功能数字钟_1_sec1 ,
       \多功能数字钟_1_sec2 ;
  wire [6:0] \多功能数字钟_1_led1 , \多功能数字钟_1_led2 , \多功能数字钟_1_led3 , \多功能数字钟_1_led4 , \多功能数字钟_1_led5 ;

  DotMatrix #(.inputtype("column"), .matrixcols(5), .matrixrows(7), .persist(0), .dotshape("square")) dotmatrix_1 (
    .col0(\多功能数字钟_1_led1 ), .col1(\多功能数字钟_1_led2 ), .col2(\多功能数字钟_1_led3 ), .col3(\多功能数字钟_1_led4 ),
    .col4(\多功能数字钟_1_led5 ));
  Button button_1 (.out(button_1_out));
  Clock #(.highDuration(1), .lowDuration(1)) clock_1 (.out(clock_1_out));
  Hex_Digit_Display hex_digit_display_1 (.value(\多功能数字钟_1_hour2 ), .dp(1'b1));
  Hex_Digit_Display hex_digit_display_2 (.value(\多功能数字钟_1_hour1 ));  // open: dp
  Button button_2 (.out(button_2_out));
  Hex_Digit_Display hex_digit_display_3 (.value(\多功能数字钟_1_min2 ), .dp(1'b1));
  Hex_Digit_Display hex_digit_display_4 (.value(\多功能数字钟_1_min1 ));  // open: dp
  Hex_Digit_Display hex_digit_display_5 (.value(\多功能数字钟_1_sec1 ));  // open: dp
  Hex_Digit_Display hex_digit_display_6 (.value(\多功能数字钟_1_sec2 ));  // open: dp
  LED #(.active("true")) led_1 (.in(\多功能数字钟_1_闹钟 ));
  \多功能数字钟  \u_多功能数字钟_1  (
    .\闹钟 (\多功能数字钟_1_闹钟 ), .led1(\多功能数字钟_1_led1 ), .led2(\多功能数字钟_1_led2 ), .led3(\多功能数字钟_1_led3 ),
    .led4(\多功能数字钟_1_led4 ), .led5(\多功能数字钟_1_led5 ), .\定点报时 (\多功能数字钟_1_定点报时 ), .Adj1(in_2), .Adj0(in_1),
    .CPu(button_1_out), .CPd(button_2_out), .Set(in_3), .Clr(in_4), .CP(clock_1_out), .Alarm_Set(in_5),
    .Alarm_On_Off(in_6), .hour1(\多功能数字钟_1_hour1 ), .hour2(\多功能数字钟_1_hour2 ), .min1(\多功能数字钟_1_min1 ),
    .min2(\多功能数字钟_1_min2 ), .sec1(\多功能数字钟_1_sec1 ), .sec2(\多功能数字钟_1_sec2 ));
  LED #(.active("true")) led_2 (.in(\多功能数字钟_1_定点报时 ));
endmodule

module \闹钟  (
  input  [3:0] Sec1,
  input  On_Off,
  input  [3:0] Hour1,
  input  [3:0] Hour2,
  input  [3:0] Min1,
  input  [3:0] Min2,
  input  Alarm_Set,
  input  CPU,
  input  Adj1,
  input  Set,
  input  CPD,
  output Alarm_out,
  output out_13,
  output out_14,
  output out_15,
  output out_16,
  output out_17,
  output out_18,
  output out_19,
  output out_20,
  output out_21,
  output out_22,
  output out_23,
  output out_24,
  output out_25,
  output out_26,
  output out_27,
  output out_28,
  output nQcc
);

  wire and_1_out, and_2_out, and_3_out, and_4_out, and_5_out, and_6_out, and_7_out, comparator_1_eq,
       comparator_2_eq, comparator_3_eq, comparator_4_eq, comparator_5_eq, not_1_out, not_2_out;

  not not_1 (not_1_out, Adj1);
  and and_1 (and_1_out, not_1_out, CPU);
  and and_2 (and_2_out, and_1_out, Alarm_Set);
  and and_3 (and_3_out, and_4_out, not_2_out);
  and and_4 (and_4_out, Alarm_Set, CPD);
  not not_2 (not_2_out, Adj1);
  Comparator #(.width(4), .mode("unsigned")) comparator_1 (
    .a(Hour1), .b({out_13, out_14, out_15, out_16}), .eq(comparator_1_eq));  // open: gt, lt
  \十二进制计数器或二十四进制的计数器电路  \u_十二进制计数器或二十四进制的计数器电路_1  (
    .CPu(and_2_out), .CPd(and_3_out), .Adj(1'b1), .Q1D(out_13), .Q1C(out_14), .Q1B(out_15), .Q1A(out_16),
    .Q0D(out_17), .Q0C(out_18), .Q0B(out_19), .Q0A(out_20), .Set(Set), .nQCC(nQcc));  // open: Clr
  and and_5 (and_5_out, Adj1, CPU);
  and and_6 (and_6_out, and_5_out, Alarm_Set);
  and and_7 (and_7_out, Adj1, and_4_out);
  Comparator #(.width(4), .mode("unsigned")) comparator_2 (
    .a(Hour2), .b({out_17, out_18, out_19, out_20}), .eq(comparator_2_eq));  // open: gt, lt
  Comparator #(.width(4), .mode("unsigned")) comparator_3 (
    .a(Sec1), .b(4'b0000), .eq(comparator_3_eq));  // open: gt, lt
  Comparator #(.width(4), .mode("unsigned")) comparator_4 (
    .a(Min1), .b({out_21, out_22, out_23, out_24}), .eq(comparator_4_eq));  // open: gt, lt
  \六十进制计数器  \u_六十进制计数器_1  (
    .Q1D(out_21), .Q1C(out_22), .Q1B(out_23), .Q1A(out_24), .Q0D(out_25), .Q0C(out_26), .Q0B(out_27),
    .Q0A(out_28), .CPu(and_6_out), .CPd(and_7_out), .Adj(1'b1));  // open: Clr, nQCC
  Comparator #(.width(4), .mode("unsigned")) comparator_5 (
    .a(Min2), .b({out_25, out_26, out_27, out_28}), .eq(comparator_5_eq));  // open: gt, lt
  and and_8 (Alarm_out, comparator_3_eq, comparator_1_eq, comparator_2_eq, On_Off, comparator_4_eq, comparator_5_eq);
endmodule

module \闹钟测试  (
  input  \闹钟开_关 ,
  input  \闹钟时间设置开_关 ,
  input  in_3,
  input  in_4,
  input  in_5,
  input  \闹钟时间设置 ,
  input  [3:0] in_7,
  input  [3:0] in_8,
  input  [3:0] in_9,
  input  [3:0] in_10,
  input  [3:0] in_11,
  output out_12
);

  wire \闹钟_1_alarm_out ;
  wire [3:0] \闹钟_1_out_16 , \闹钟_1_out_20 , \闹钟_1_out_24 , \闹钟_1_out_28 ;

  Hex_Digit_Display hex_digit_display_1 (.value(\闹钟_1_out_16 ));  // open: dp
  \闹钟  \u_闹钟_1  (
    .Alarm_Set(\闹钟时间设置开_关 ), .Set(in_3), .CPU(in_5), .Adj1(in_4), .out_13(\闹钟_1_out_16 [3]),
    .out_14(\闹钟_1_out_16 [2]), .out_15(\闹钟_1_out_16 [1]), .out_16(\闹钟_1_out_16 [0]),
    .out_17(\闹钟_1_out_20 [3]), .out_18(\闹钟_1_out_20 [2]), .out_19(\闹钟_1_out_20 [1]),
    .out_20(\闹钟_1_out_20 [0]), .out_21(\闹钟_1_out_24 [3]), .out_22(\闹钟_1_out_24 [2]),
    .out_23(\闹钟_1_out_24 [1]), .out_24(\闹钟_1_out_24 [0]), .out_25(\闹钟_1_out_28 [3]),
    .out_26(\闹钟_1_out_28 [2]), .out_27(\闹钟_1_out_28 [1]), .out_28(\闹钟_1_out_28 [0]), .On_Off(\闹钟开_关 ),
    .Alarm_out(\闹钟_1_alarm_out ), .CPD(\闹钟时间设置 ), .Hour1(in_7), .Hour2(in_8), .Min1(in_9), .Min2(in_10),
    .Sec1(in_11), .nQcc(out_12));
  Hex_Digit_Display hex_digit_display_2 (.value(\闹钟_1_out_20 ), .dp(1'b1));
  Hex_Digit_Display hex_digit_display_3 (.value(\闹钟_1_out_24 ));  // open: dp
  Hex_Digit_Display hex_digit_display_4 (.value(\闹钟_1_out_28 ));  // open: dp
  LED #(.active("true")) led_1 (.in(\闹钟_1_alarm_out ));

  // Notes on the sheet:
  //   闹钟状态 0、12小时制 1、24小时制
  //   闹钟设置 0、小时 1、分钟
endmodule
