// Logisim project 实验6-ACM1801-U201814757-夏媛.circ as structural Verilog: 5 circuits, main circuit sqrX
module sqrX (
  input  [31:0] a,
  input  [31:0] b,
  input  [31:0] c,
  input  [31:0] d,
  output [31:0] a_prime,
  output [31:0] b_prime,
  output [31:0] c_prime,
  output [31:0] d_prime
);

  wire [31:0] multiplier_1_out, multiplier_2_out, multiplier_3_out, multiplier_4_out, multiplier_5_out,
       multiplier_6_out, multiplier_7_out, multiplier_8_out;

  Multiplier #(.width(32)) multiplier_1 (.a(a), .b(a), .out(multiplier_1_out), .cin({32{1'b0}}));  // open: cout
  Multiplier #(.width(32)) multiplier_2 (.a(a), .b(b), .out(multiplier_2_out), .cin({32{1'b0}}));  // open: cout
  Multiplier #(.width(32)) multiplier_3 (.a(b), .b(c), .out(multiplier_3_out), .cin({32{1'b0}}));  // open: cout
  Multiplier #(.width(32)) multiplier_4 (.a(b), .b(d), .out(multiplier_4_out), .cin({32{1'b0}}));  // open: cout
  Multiplier #(.width(32)) multiplier_5 (.a(a), .b(c), .out(multiplier_5_out), .cin({32{1'b0}}));  // open: cout
  Multiplier #(.width(32)) multiplier_6 (.a(c), .b(d), .out(multiplier_6_out), .cin({32{1'b0}}));  // open: cout
  Multiplier #(.width(32)) multiplier_7 (.a(c), .b(b), .out(multiplier_7_out), .cin({32{1'b0}}));  // open: cout
  Multiplier #(.width(32)) multiplier_8 (.a(d), .b(d), .out(multiplier_8_out), .cin({32{1'b0}}));  // open: cout
  Adder #(.width(32)) adder_1 (.a(multiplier_1_out), .b(multiplier_3_out), .out(a_prime), .cin(1'b0));  // open: cout
  Adder #(.width(32)) adder_2 (.a(multiplier_2_out), .b(multiplier_4_out), .out(b_prime), .cin(1'b0));  // open: cout
  Adder #(.width(32)) adder_3 (.a(multiplier_5_out), .b(multiplier_6_out), .out(c_prime), .cin(1'b0));  // open: cout
  Adder #(.width(32)) adder_4 (.a(multiplier_7_out), .b(multiplier_8_out), .out(d_prime), .cin(1'b0));  // open: cout
endmodule

module sqrX_A (
  input  [31:0] in_1,
  input  [31:0] in_2,
  input  [31:0] in_3,
  input  [31:0] in_4,
  output [31:0] b_prime_prime,
  output [31:0] a_prime_prime,
  output [31:0] c_prime_prime,
  output [31:0] d_prime_prime
);

  wire [31:0] sqrx_1_a_prime, sqrx_1_c_prime;

  sqrX sqrx_1 (
    .a(in_1), .b(in_2), .c(in_3), .d(in_4), .a_prime(sqrx_1_a_prime), .b_prime(a_prime_prime),
    .c_prime(sqrx_1_c_prime), .d_prime(c_prime_prime));
  Adder #(.width(32)) adder_1 (.a(sqrx_1_a_prime), .b(a_prime_prime), .out(b_prime_prime), .cin(1'b0));  // open: cout
  Adder #(.width(32)) adder_2 (.a(c_prime_prime), .b(sqrx_1_c_prime), .out(d_prime_prime), .cin(1'b0));  // open: cout
endmodule

module \Fibonacci数显示模块  (
  input  [31:0] in_1,
  output [3:0] out_2,
  output [3:0] out_3,
  output [3:0] out_4,
  output [3:0] out_5,
  output [3:0] out_6,
  output [3:0] out_7,
  output [3:0] out_8,
  output [3:0] out_9,
  output [3:0] out_10,
  output [3:0] out_11
);

  wire [3:0] divider_1_rem_2, divider_1_rem_3, divider_1_rem_4, divider_1_rem_5, divider_2_rem_2,
       divider_2_rem_3, divider_2_rem_4, divider_2_rem_5, divider_3_rem_2, divider_3_rem_3, divider_3_rem_4,
       divider_3_rem_5, divider_4_rem_2, divider_4_rem_3, divider_4_rem_4, divider_4_rem_5, divider_5_rem_2,
       divider_5_rem_3, divider_5_rem_4, divider_5_rem_5, divider_6_rem_2, divider_6_rem_3, divider_6_rem_4,
       divider_6_rem_5, divider_7_rem_2, divider_7_rem_3, divider_8_rem_2, divider_8_rem_3, divider_8_rem_4,
       divider_8_rem_5, divider_9_rem_2, divider_9_rem_3, divider_9_rem_4, divider_9_rem_5, divider_10_rem_2,
       divider_10_rem_3, divider_10_rem_4, divider_10_rem_5;
  wire [15:4] divider_1_rem, divider_2_rem, divider_3_rem, divider_4_rem, divider_5_rem, divider_6_rem,
       divider_8_rem, divider_9_rem, divider_10_rem;
  wire [31:0] divider_1_out, divider_2_out, divider_3_out, divider_4_out, divider_5_out, divider_6_out,
       divider_7_out, divider_8_out, divider_9_out;
  wire [31:4] divider_7_rem;

  Divider #(.width(32)) divider_1 (
    .a(in_1), .b(32'ha), .out(divider_1_out), .upper({32{1'b0}}),
    .rem({divider_1_rem_5, divider_1_rem_4, divider_1_rem_3, divider_1_rem_2, divider_1_rem, out_2}));
  Divider #(.width(32)) divider_2 (
    .a(divider_1_out), .b(32'ha), .out(divider_2_out), .upper({32{1'b0}}),
    .rem({divider_2_rem_5, divider_2_rem_4, divider_2_rem_3, divider_2_rem_2, divider_2_rem, out_3}));
  Divider #(.width(32)) divider_3 (
    .a(divider_2_out), .b(32'ha), .out(divider_3_out), .upper({32{1'b0}}),
    .rem({divider_3_rem_5, divider_3_rem_4, divider_3_rem_3, divider_3_rem_2, divider_3_rem, out_4}));
  Divider #(.width(32)) divider_4 (
    .a(divider_3_out), .b(32'ha), .out(divider_4_out), .upper({32{1'b0}}),
    .rem({divider_4_rem_5, divider_4_rem_4, divider_4_rem_3, divider_4_rem_2, divider_4_rem, out_5}));
  Divider #(.width(32)) divider_5 (
    .a(divider_4_out), .b(32'ha), .out(divider_5_out), .upper({32{1'b0}}),
    .rem({divider_5_rem_5, divider_5_rem_4, divider_5_rem_3, divider_5_rem_2, divider_5_rem, out_6}));
  Divider #(.width(32)) divider_6 (
    .a(divider_5_out), .b(32'ha), .out(divider_6_out), .upper({32{1'b0}}),
    .rem({divider_6_rem_5, divider_6_rem_4, divider_6_rem_3, divider_6_rem_2, divider_6_rem, out_7}));
  Divider #(.width(32)) divider_7 (
    .a(divider_6_out), .b(32'ha), .out(divider_7_out), .upper({32{1'b0}}),
    .rem({divider_7_rem[31:24], divider_7_rem_3, divider_7_rem_2, divider_7_rem[15:4], out_8}));
  Divider #(.width(32)) divider_8 (
    .a(divider_7_out), .b(32'ha), .out(divider_8_out), .upper({32{1'b0}}),
    .rem({divider_8_rem_5, divider_8_rem_4, divider_8_rem_3, divider_8_rem_2, divider_8_rem, out_9}));
  Divider #(.width(32)) divider_9 (
    .a(divider_8_out), .b(32'ha), .out(divider_9_out), .upper({32{1'b0}}),
    .rem({divider_9_rem_5, divider_9_rem_4, divider_9_rem_3, divider_9_rem_2, divider_9_rem, out_10}));
  Divider #(.width(32)) divider_10 (
    .a(divider_9_out), .b(32'ha), .upper({32{1'b0}}),
    .rem({divider_10_rem_5, divider_10_rem_4, divider_10_rem_3, divider_10_rem_2, divider_10_rem, out_11}));  // open: out
endmodule

module \斐波那契_Fibonacci_数列计算器  (
  input  [5:0] n,
  input  clear,
  input  clk,
  output [3:0] out_4,
  output [3:0] out_5,
  output [3:0] out_6,
  output [3:0] out_7,
  output [3:0] out_8,
  output [3:0] out_9,
  output [3:0] out_10,
  output [3:0] out_11,
  output [3:0] out_12,
  output [3:0] out_13
);

  wire and_1_out, comparator_1_lt, d_ff_1_q, not_1_out, or_1_out, or_2_out, or_3_out, shift_register_1_out,
       shift_register_1_q6;
  wire [7:0] counter_1_q;
  wire [31:0] multiplexer_1_out, multiplexer_2_out, multiplexer_3_out, multiplexer_4_out, multiplexer_5_out,
       multiplexer_6_out, multiplexer_7_out, multiplexer_8_out, register_1_q, register_2_q, register_3_q,
       register_4_q, sqrx_1_a_prime, sqrx_1_b_prime, sqrx_1_c_prime, sqrx_1_d_prime, sqrx_a_1_a_prime_prime,
       sqrx_a_1_b_prime_prime, sqrx_a_1_c_prime_prime, sqrx_a_1_d_prime_prime;

  Counter #(.width(8), .max('hff), .ongoal("wrap"), .trigger("rising"), .behavior("old")) counter_1 (
    .load(1'b0), .D({8{1'b0}}), .count(1'b1), .Q(counter_1_q), .clk(clk), .clr(clear));  // open: carry, preset
  Comparator #(.width(8), .mode("twosComplement")) comparator_1 (
    .a(counter_1_q), .b(8'h6), .lt(comparator_1_lt));  // open: gt, eq
  not not_1 (not_1_out, clear);
  Shift_Register #(.width(1), .length(7), .parallel("true"), .trigger("rising")) shift_register_1 (
    .shift(not_1_out), .in(1'b0), .clk(or_1_out), .out(shift_register_1_out), .load(clear), .clr(1'b0),
    .d0(n[0]), .d1(n[1]), .d2(n[2]), .d3(n[3]), .d4(n[4]), .d5(n[5]), .d6(1'b0), .q6(shift_register_1_q6));  // open: q0, q1, q2, q3, q4, q5
  and and_1 (and_1_out, comparator_1_lt, clk);
  or or_1 (or_1_out, and_1_out, clear);
  or or_2 (or_2_out, shift_register_1_q6, d_ff_1_q);
  D_Flip_Flop #(.trigger("falling"), .Pre_Clr_Positions("LEGACY"), .NegatePresetClear("false"), .enable("true"), .NewFFLayout("false")) d_ff_1 (
    .clk(or_1_out), .D(or_2_out), .Q(d_ff_1_q), .preset(1'b0), .en(1'b1), .reset(clear));  // open: Qn
  Multiplexer #(.select(1), .width(32), .disabled("Z"), .enable("false")) multiplexer_1 (
    .in0({32{1'b0}}), .in1(multiplexer_5_out), .out(multiplexer_1_out), .sel(d_ff_1_q));
  Multiplexer #(.select(1), .width(32), .disabled("Z"), .enable("false")) multiplexer_2 (
    .in0(32'h1), .in1(multiplexer_6_out), .out(multiplexer_2_out), .sel(d_ff_1_q));
  Multiplexer #(.select(1), .width(32), .disabled("Z"), .enable("false")) multiplexer_3 (
    .in0(32'h1), .in1(multiplexer_7_out), .out(multiplexer_3_out), .sel(d_ff_1_q));
  Multiplexer #(.select(1), .width(32), .disabled("Z"), .enable("false")) multiplexer_4 (
    .in0(32'h1), .in1(multiplexer_8_out), .out(multiplexer_4_out), .sel(d_ff_1_q));
  Register #(.width(32), .trigger("falling"), .Select("low")) register_1 (
    .D(multiplexer_1_out), .en(1'b1), .Q(register_1_q), .clk(or_3_out), .clr(1'b0));
  Register #(.width(32), .trigger("falling"), .Select("low")) register_2 (
    .D(multiplexer_2_out), .en(1'b1), .Q(register_2_q), .clk(or_3_out), .clr(1'b0));
  Register #(.width(32), .trigger("falling"), .Select("low")) register_3 (
    .D(multiplexer_3_out), .en(1'b1), .Q(register_3_q), .clk(or_3_out), .clr(1'b0));
  Register #(.width(32), .trigger("falling"), .Select("low")) register_4 (
    .D(multiplexer_4_out), .en(1'b1), .Q(register_4_q), .clk(or_3_out), .clr(1'b0));
  or or_3 (or_3_out, clear, or_1_out);
  sqrX sqrx_1 (
    .a(register_1_q), .b(register_2_q), .c(register_3_q), .d(register_4_q), .a_prime(sqrx_1_a_prime),
    .b_prime(sqrx_1_b_prime), .c_prime(sqrx_1_c_prime), .d_prime(sqrx_1_d_prime));
  sqrX_A sqrx_a_1 (
    .in_1(register_1_q), .in_2(register_2_q), .in_3(register_3_q), .in_4(register_4_q),
    .b_prime_prime(sqrx_a_1_b_prime_prime), .a_prime_prime(sqrx_a_1_a_prime_prime),
    .c_prime_prime(sqrx_a_1_c_prime_prime), .d_prime_prime(sqrx_a_1_d_prime_prime));
  Multiplexer #(.select(1), .width(32), .disabled("Z"), .enable("false")) multiplexer_5 (
    .in0(sqrx_1_a_prime), .in1(sqrx_a_1_a_prime_prime), .out(multiplexer_5_out), .sel(shift_register_1_out));
  Multiplexer #(.select(1), .width(32), .disabled(0), .enable("false")) multiplexer_6 (
    .in0(sqrx_1_b_prime), .in1(sqrx_a_1_b_prime_prime), .out(multiplexer_6_out), .sel(shift_register_1_out));
  Multiplexer #(.select(1), .width(32), .disabled("Z"), .enable("false")) multiplexer_7 (
    .in0(sqrx_1_c_prime), .in1(sqrx_a_1_c_prime_prime), .out(multiplexer_7_out), .sel(shift_register_1_out));
  Multiplexer #(.select(1), .width(32), .disabled("Z"), .enable("false")) multiplexer_8 (
    .in0(sqrx_1_d_prime), .in1(sqrx_a_1_d_prime_prime), .out(multiplexer_8_out), .sel(shift_register_1_out));
  \Fibonacci数显示模块  \fibonacci数显示模块_1  (
    .in_1(register_2_q), .out_2(out_13), .out_3(out_12), .out_4(out_11), .out_5(out_10), .out_6(out_9),
    .out_7(out_8), .out_8(out_7), .out_9(out_6), .out_10(out_5), .out_11(out_4));
endmodule

module \斐波那契_Fibonacci_数列计算器验证电路  (
  input  [5:0] in_1
);

  wire button_1_out, button_2_out;
  wire [3:0] \斐波那契_fibonacci_数列计算器_1_out_4 , \斐波那契_fibonacci_数列计算器_1_out_5 , \斐波那契_fibonacci_数列计算器_1_out_6 ,
       \斐波那契_fibonacci_数列计算器_1_out_7 , \斐波那契_fibonacci_数列计算器_1_out_8 , \斐波那契_fibonacci_数列计算器_1_out_9 ,
       \斐波那契_fibonacci_数列计算器_1_out_10 , \斐波那契_fibonacci_数列计算器_1_out_11 , \斐波那契_fibonacci_数列计算器_1_out_12 ,
       \斐波那契_fibonacci_数列计算器_1_out_13 ;

  Button button_1 (.out(button_1_out));
  Button button_2 (.out(button_2_out));
  \斐波那契_Fibonacci_数列计算器  \u_斐波那契_fibonacci_数列计算器_1  (
    .clear(button_1_out), .out_4(\斐波那契_fibonacci_数列计算器_1_out_4 ), .out_5(\斐波那契_fibonacci_数列计算器_1_out_5 ),
    .out_6(\斐波那契_fibonacci_数列计算器_1_out_6 ), .out_7(\斐波那契_fibonacci_数列计算器_1_out_7 ),
    .out_8(\斐波那契_fibonacci_数列计算器_1_out_8 ), .out_9(\斐波那契_fibonacci_数列计算器_1_out_9 ),
    .out_10(\斐波那契_fibonacci_数列计算器_1_out_10 ), .out_11(\斐波那契_fibonacci_数列计算器_1_out_11 ),
    .out_12(\斐波那契_fibonacci_数列计算器_1_out_12 ), .out_13(\斐波那契_fibonacci_数列计算器_1_out_13 ), .n(in_1),
    .clk(button_2_out));
  Hex_Digit_Display hex_digit_display_1 (.value(\斐波那契_fibonacci_数列计算器_1_out_4 ));  // open: dp
  Hex_Digit_Display hex_digit_display_2 (.value(\斐波那契_fibonacci_数列计算器_1_out_5 ));  // open: dp
  Hex_Digit_Display hex_digit_display_3 (.value(\斐波那契_fibonacci_数列计算器_1_out_7 ));  // open: dp
  Hex_Digit_Display hex_digit_display_4 (.value(\斐波那契_fibonacci_数列计算器_1_out_6 ));  // open: dp
  Hex_Digit_Display hex_digit_display_5 (.value(\斐波那契_fibonacci_数列计算器_1_out_9 ));  // open: dp
  Hex_Digit_Display hex_digit_display_6 (.value(\斐波那契_fibonacci_数列计算器_1_out_8 ));  // open: dp
  Hex_Digit_Display hex_digit_display_7 (.value(\斐波那契_fibonacci_数列计算器_1_out_10 ));  // open: dp
  Hex_Digit_Display hex_digit_display_8 (.value(\斐波那契_fibonacci_数列计算器_1_out_11 ));  // open: dp
  Hex_Digit_Display hex_digit_display_9 (.value(\斐波那契_fibonacci_数列计算器_1_out_12 ));  // open: dp
  Hex_Digit_Display hex_digit_display_10 (.value(\斐波那契_fibonacci_数列计算器_1_out_13 ));  // open: dp

  // Notes on the sheet:
  //   注：n改变后，将clear置1再置0
endmodule
