// Logisim project 实验6-CS1804-U201814755-彭子晨.circ as structural Verilog: 5 circuits, main circuit sqrX
module sqrX (
  input  [31:0] a,
  input  [31:0] b,
  input  [31:0] c,
  input  [31:0] d,
  output [31:0] a_prime,
  output [31:0] b_prime,
  output [31:0] c_prime,
  output [31:0] d_prime
);

  wire [31:0] multiplier_1_out, multiplier_2_out, multiplier_3_out, multiplier_4_out, multiplier_5_out,
       multiplier_6_out, multiplier_7_out, multiplier_8_out;

  Multiplier #(.width(32)) multiplier_1 (.a(a), .b(a), .out(multiplier_1_out));  // open: cin, cout
  Multiplier #(.width(32)) multiplier_2 (.a(a), .b(b), .out(multiplier_2_out));  // open: cin, cout
  Multiplier #(.width(32)) multiplier_3 (.a(b), .b(c), .out(multiplier_3_out));  // open: cin, cout
  Multiplier #(.width(32)) multiplier_4 (.a(b), .b(d), .out(multiplier_4_out));  // open: cin, cout
  Multiplier #(.width(32)) multiplier_5 (.a(a), .b(c), .out(multiplier_5_out));  // open: cin, cout
  Multiplier #(.width(32)) multiplier_6 (.a(c), .b(d), .out(multiplier_6_out));  // open: cin, cout
  Multiplier #(.width(32)) multiplier_7 (.a(b), .b(c), .out(multiplier_7_out));  // open: cin, cout
  Multiplier #(.width(32)) multiplier_8 (.a(d), .b(d), .out(multiplier_8_out));  // open: cin, cout
  Adder #(.width(32)) adder_1 (.a(multiplier_1_out), .b(multiplier_3_out), .out(a_prime));  // open: cin, cout
  Adder #(.width(32)) adder_2 (.a(multiplier_2_out), .b(multiplier_4_out), .out(b_prime));  // open: cin, cout
  Adder #(.width(32)) adder_3 (.a(multiplier_5_out), .b(multiplier_6_out), .out(c_prime));  // open: cin, cout
  Adder #(.width(32)) adder_4 (.a(multiplier_7_out), .b(multiplier_8_out), .out(d_prime));  // open: cin, cout
endmodule

module sqrX_A (
  input  [31:0] a,
  input  [31:0] b,
  input  [31:0] c,
  input  [31:0] d,
  output [31:0] a_prime_prime,
  output [31:0] b_prime_prime,
  output [31:0] c_prime_prime,
  output [31:0] d_prime_prime
);

  wire [31:0] sqrx_1_a_prime, sqrx_1_c_prime;

  sqrX sqrx_1 (
    .a(a), .b(b), .c(c), .d(d), .a_prime(sqrx_1_a_prime), .b_prime(a_prime_prime), .c_prime(sqrx_1_c_prime),
    .d_prime(c_prime_prime));
  Adder #(.width(32)) adder_1 (.a(sqrx_1_a_prime), .b(a_prime_prime), .out(b_prime_prime));  // open: cin, cout
  Adder #(.width(32)) adder_2 (.a(sqrx_1_c_prime), .b(c_prime_prime), .out(d_prime_prime));  // open: cin, cout
endmodule

module \Fibonacci数显示模块  (
  input  [31:0] F,
  output [3:0] D0,
  output [3:0] D1,
  output [3:0] D2,
  output [3:0] D3,
  output [3:0] D4,
  output [3:0] D5,
  output [3:0] D6,
  output [3:0] D7,
  output [3:0] D8,
  output [3:0] D9
);

  wire [31:0] divider_1_out, divider_2_out, divider_3_out, divider_4_out, divider_5_out, divider_6_out,
       divider_7_out, divider_8_out, divider_9_out;
  wire [31:4] divider_1_rem, divider_2_rem, divider_3_rem, divider_5_rem, divider_6_rem, divider_7_rem,
       divider_8_rem, divider_9_rem, divider_10_rem;
  wire [31:8] divider_4_rem;

  Divider #(.width(32)) divider_1 (
    .a(F), .b(32'ha), .out(divider_1_out), .upper({32{1'b0}}), .rem({divider_1_rem, D0}));
  Divider #(.width(32)) divider_2 (
    .a(divider_1_out), .b(32'ha), .out(divider_2_out), .upper({32{1'b0}}), .rem({divider_2_rem, D1}));
  Divider #(.width(32)) divider_3 (
    .a(divider_2_out), .b(32'ha), .out(divider_3_out), .upper({32{1'b0}}), .rem({divider_3_rem, D2}));
  Divider #(.width(32)) divider_4 (
    .a(divider_3_out), .b(32'ha), .out(divider_4_out), .upper({32{1'b0}}),
    .rem({divider_4_rem, divider_4_rem[11:8], D3}));
  Divider #(.width(32)) divider_5 (
    .a(divider_4_out), .b(32'ha), .out(divider_5_out), .upper({32{1'b0}}), .rem({divider_5_rem, D4}));
  Divider #(.width(32)) divider_6 (
    .a(divider_5_out), .b(32'ha), .out(divider_6_out), .upper({32{1'b0}}), .rem({divider_6_rem, D5}));
  Divider #(.width(32)) divider_7 (
    .a(divider_6_out), .b(32'ha), .out(divider_7_out), .upper({32{1'b0}}), .rem({divider_7_rem, D6}));
  Divider #(.width(32)) divider_8 (
    .a(divider_7_out), .b(32'ha), .out(divider_8_out), .upper({32{1'b0}}), .rem({divider_8_rem, D7}));
  Divider #(.width(32)) divider_9 (
    .a(divider_8_out), .b(32'ha), .out(divider_9_out), .upper({32{1'b0}}), .rem({divider_9_rem, D8}));
  Divider #(.width(32)) divider_10 (
    .a(divider_9_out), .b(32'ha), .upper({32{1'b0}}), .rem({divider_10_rem, D9}));  // open: out
endmodule

module \斐波那契_Fibonacci_数列计算器  (
  input  [5:0] n,
  input  clear,
  input  clk,
  output [3:0] D9,
  output [3:0] D8,
  output [3:0] D7,
  output [3:0] D6,
  output [3:0] D5,
  output [3:0] D4,
  output [3:0] D3,
  output [3:0] D2,
  output [3:0] D1,
  output [3:0] D0
);

  wire and_1_out, comparator_1_lt, d_ff_1_q, not_1_out, or_1_out, or_2_out, or_3_out, shift_register_1_out,
       shift_register_1_q6;
  wire [7:0] counter_1_q;
  wire [31:0] multiplexer_1_out, multiplexer_2_out, multiplexer_3_out, multiplexer_4_out, multiplexer_5_out,
       multiplexer_6_out, multiplexer_7_out, multiplexer_8_out, register_1_q, register_2_q, register_3_q,
       register_4_q, sqrx_1_a_prime, sqrx_1_b_prime, sqrx_1_c_prime, sqrx_1_d_prime, sqrx_a_1_a_prime_prime,
       sqrx_a_1_b_prime_prime, sqrx_a_1_c_prime_prime, sqrx_a_1_d_prime_prime;

  Counter #(.width(8), .max('hff), .ongoal("wrap"), .trigger("rising"), .behavior("old")) counter_1 (
    .load(1'b0), .D({8{1'b0}}), .count(1'b1), .Q(counter_1_q), .clk(clk), .clr(clear));  // open: carry, preset
  Comparator #(.width(8), .mode("twosComplement")) comparator_1 (
    .a(counter_1_q), .b(8'h6), .lt(comparator_1_lt));  // open: gt, eq
  not not_1 (not_1_out, clear);
  Shift_Register #(.width(1), .length(7), .parallel("true"), .trigger("rising")) shift_register_1 (
    .shift(not_1_out), .in(1'b0), .clk(or_1_out), .out(shift_register_1_out), .load(clear), .clr(1'b0),
    .d0(n[0]), .d1(n[1]), .d2(n[2]), .d3(n[3]), .d4(n[4]), .d5(n[5]), .d6(1'b0), .q6(shift_register_1_q6));  // open: q0, q1, q2, q3, q4, q5
  and and_1 (and_1_out, comparator_1_lt, clk);
  or or_1 (or_1_out, and_1_out, clear);
  or or_2 (or_2_out, shift_register_1_q6, d_ff_1_q);
  Multiplexer #(.select(1), .width(32), .disabled("Z"), .enable("false")) multiplexer_1 (
    .in0(32'h1), .in1(multiplexer_7_out), .out(multiplexer_1_out), .sel(d_ff_1_q));
  Multiplexer #(.select(1), .width(32), .disabled("Z"), .enable("false")) multiplexer_2 (
    .in0(32'h1), .in1(multiplexer_8_out), .out(multiplexer_2_out), .sel(d_ff_1_q));
  D_Flip_Flop #(.trigger("falling"), .Pre_Clr_Positions("LEGACY"), .NegatePresetClear("false"), .enable("true"), .NewFFLayout("false")) d_ff_1 (
    .clk(or_1_out), .D(or_2_out), .Q(d_ff_1_q), .preset(1'b0), .en(1'b1), .reset(clear));  // open: Qn
  Multiplexer #(.select(1), .width(32), .disabled("Z"), .enable("false")) multiplexer_3 (
    .in0({32{1'b0}}), .in1(multiplexer_5_out), .out(multiplexer_3_out), .sel(d_ff_1_q));
  Multiplexer #(.select(1), .width(32), .disabled("Z"), .enable("false")) multiplexer_4 (
    .in0(32'h1), .in1(multiplexer_6_out), .out(multiplexer_4_out), .sel(d_ff_1_q));
  or or_3 (or_3_out, or_1_out, clear);
  Register #(.width(32), .trigger("falling"), .Select("low")) register_1 (
    .D(multiplexer_3_out), .en(1'b1), .Q(register_1_q), .clk(or_3_out), .clr(1'b0));
  Register #(.width(32), .trigger("falling"), .Select("low")) register_2 (
    .D(multiplexer_4_out), .en(1'b1), .Q(register_2_q), .clk(or_3_out), .clr(1'b0));
  Register #(.width(32), .trigger("falling"), .Select("low")) register_3 (
    .D(multiplexer_1_out), .en(1'b1), .Q(register_3_q), .clk(or_3_out), .clr(1'b0));
  Register #(.width(32), .trigger("falling"), .Select("low")) register_4 (
    .D(multiplexer_2_out), .en(1'b1), .Q(register_4_q), .clk(or_3_out), .clr(1'b0));
  sqrX sqrx_1 (
    .a(register_1_q), .b(register_2_q), .c(register_3_q), .d(register_4_q), .a_prime(sqrx_1_a_prime),
    .b_prime(sqrx_1_b_prime), .c_prime(sqrx_1_c_prime), .d_prime(sqrx_1_d_prime));
  sqrX_A sqrx_a_1 (
    .a(register_1_q), .b(register_2_q), .c(register_3_q), .d(register_4_q),
    .a_prime_prime(sqrx_a_1_a_prime_prime), .b_prime_prime(sqrx_a_1_b_prime_prime),
    .c_prime_prime(sqrx_a_1_c_prime_prime), .d_prime_prime(sqrx_a_1_d_prime_prime));
  Multiplexer #(.select(1), .width(32), .disabled("Z"), .enable("false")) multiplexer_5 (
    .in0(sqrx_1_a_prime), .in1(sqrx_a_1_a_prime_prime), .out(multiplexer_5_out), .sel(shift_register_1_out));
  Multiplexer #(.select(1), .width(32), .disabled("Z"), .enable("false")) multiplexer_6 (
    .in0(sqrx_1_b_prime), .in1(sqrx_a_1_b_prime_prime), .out(multiplexer_6_out), .sel(shift_register_1_out));
  Multiplexer #(.select(1), .width(32), .disabled("Z"), .enable("false")) multiplexer_7 (
    .in0(sqrx_1_c_prime), .in1(sqrx_a_1_c_prime_prime), .out(multiplexer_7_out), .sel(shift_register_1_out));
  Multiplexer #(.select(1), .width(32), .disabled("Z"), .enable("false")) multiplexer_8 (
    .in0(sqrx_1_d_prime), .in1(sqrx_a_1_d_prime_prime), .out(multiplexer_8_out), .sel(shift_register_1_out));
  \Fibonacci数显示模块  \fibonacci数显示模块_1  (
    .D0(D0), .D1(D1), .D2(D2), .D3(D3), .D4(D4), .D5(D5), .D6(D6), .D7(D7), .D8(D8), .D9(D9), .F(register_2_q));
endmodule

module \斐波那契_Fibonacci_数列计算器验证电路  (
  input  [5:0] in_1
);

  wire button_1_out, button_2_out;
  wire [3:0] \斐波那契_fibonacci_数列计算器_1_d0 , \斐波那契_fibonacci_数列计算器_1_d1 , \斐波那契_fibonacci_数列计算器_1_d2 ,
       \斐波那契_fibonacci_数列计算器_1_d3 , \斐波那契_fibonacci_数列计算器_1_d4 , \斐波那契_fibonacci_数列计算器_1_d5 ,
       \斐波那契_fibonacci_数列计算器_1_d6 , \斐波那契_fibonacci_数列计算器_1_d7 , \斐波那契_fibonacci_数列计算器_1_d8 ,
       \斐波那契_fibonacci_数列计算器_1_d9 ;

  Button button_1 (.out(button_1_out));
  Button button_2 (.out(button_2_out));
  Hex_Digit_Display hex_digit_display_1 (.value(\斐波那契_fibonacci_数列计算器_1_d9 ));  // open: dp
  \斐波那契_Fibonacci_数列计算器  \u_斐波那契_fibonacci_数列计算器_1  (
    .clear(button_1_out), .clk(button_2_out), .D9(\斐波那契_fibonacci_数列计算器_1_d9 ),
    .D8(\斐波那契_fibonacci_数列计算器_1_d8 ), .D7(\斐波那契_fibonacci_数列计算器_1_d7 ), .D6(\斐波那契_fibonacci_数列计算器_1_d6 ),
    .D5(\斐波那契_fibonacci_数列计算器_1_d5 ), .D4(\斐波那契_fibonacci_数列计算器_1_d4 ), .D3(\斐波那契_fibonacci_数列计算器_1_d3 ),
    .D2(\斐波那契_fibonacci_数列计算器_1_d2 ), .D1(\斐波那契_fibonacci_数列计算器_1_d1 ), .D0(\斐波那契_fibonacci_数列计算器_1_d0 ),
    .n(in_1));
  Hex_Digit_Display hex_digit_display_2 (.value(\斐波那契_fibonacci_数列计算器_1_d8 ));  // open: dp
  Hex_Digit_Display hex_digit_display_3 (.value(\斐波那契_fibonacci_数列计算器_1_d7 ));  // open: dp
  Hex_Digit_Display hex_digit_display_4 (.value(\斐波那契_fibonacci_数列计算器_1_d6 ));  // open: dp
  Hex_Digit_Display hex_digit_display_5 (.value(\斐波那契_fibonacci_数列计算器_1_d5 ));  // open: dp
  Hex_Digit_Display hex_digit_display_6 (.value(\斐波那契_fibonacci_数列计算器_1_d4 ));  // open: dp
  Hex_Digit_Display hex_digit_display_7 (.value(\斐波那契_fibonacci_数列计算器_1_d3 ));  // open: dp
  Hex_Digit_Display hex_digit_display_8 (.value(\斐波那契_fibonacci_数列计算器_1_d2 ));  // open: dp
  Hex_Digit_Display hex_digit_display_9 (.value(\斐波那契_fibonacci_数列计算器_1_d1 ));  // open: dp
  Hex_Digit_Display hex_digit_display_10 (.value(\斐波那契_fibonacci_数列计算器_1_d0 ));  // open: dp
endmodule
