// Logisim project RGLED.circ as structural Verilog
module \数码管驱动  (
  input  X3,
  input  X2,
  input  X1,
  input  X0,
  output Seg_1,
  output Seg_2,
  output Seg_3,
  output Seg_4,
  output Seg_5,
  output Seg_6,
  output Seg_7
);
endmodule

module \数码管驱动测试  (
);

  wire clock_1_out, \数码管驱动_1_seg_1 , \数码管驱动_1_seg_2 , \数码管驱动_1_seg_3 , \数码管驱动_1_seg_4 , \数码管驱动_1_seg_5 ,
       \数码管驱动_1_seg_6 , \数码管驱动_1_seg_7 ;
  wire [3:0] counter_1_q;

  Counter #(.width(4), .max('hf), .ongoal("wrap"), .trigger("rising"), .behavior("old")) counter_1 (
    .Q(counter_1_q), .clk(clock_1_out));  // open: load, D, count, carry, clr, preset
  Clock #(.highDuration(1), .lowDuration(1)) clock_1 (.out(clock_1_out));
  \数码管驱动  \u_数码管驱动_1  (
    .X3(counter_1_q[3]), .Seg_1(\数码管驱动_1_seg_1 ), .X2(counter_1_q[2]), .Seg_2(\数码管驱动_1_seg_2 ),
    .X1(counter_1_q[1]), .Seg_3(\数码管驱动_1_seg_3 ), .X0(counter_1_q[0]), .Seg_4(\数码管驱动_1_seg_4 ),
    .Seg_5(\数码管驱动_1_seg_5 ), .Seg_6(\数码管驱动_1_seg_6 ), .Seg_7(\数码管驱动_1_seg_7 ));
  _7_Segment_Display #(.active("true")) u_7_segment_display_1 (
    .g(\数码管驱动_1_seg_1 ), .f(\数码管驱动_1_seg_2 ), .a(\数码管驱动_1_seg_3 ), .b(\数码管驱动_1_seg_4 ), .e(\数码管驱动_1_seg_5 ),
    .d(\数码管驱动_1_seg_6 ), .c(\数码管驱动_1_seg_7 ));  // open: dp

  // Notes on the sheet:
  //   Ctrl+T驱动时钟单步运行测试
endmodule

// 4位数比较器
module \_4位无符号比较器  (
  input  X3,
  input  X2,
  input  X1,
  input  X0,
  input  Y3,
  input  Y2,
  input  Y1,
  input  Y0,
  output Great,
  output Equal,
  output Less
);
endmodule

module \_8位无符号比较器  (
  input  [7:0] X,
  input  [7:0] Y,
  output Great,
  output Equal,
  output Less
);

  // Probe on X
  // Probe on Y
  \_4位无符号比较器  \u_4位无符号比较器_1  ();  // open: X3, X2, X1, X0, Y3, Y2, Y1, Y0, Great, Equal, Less
  \_4位无符号比较器  \u_4位无符号比较器_2  ();  // open: X3, X2, X1, X0, Y3, Y2, Y1, Y0, Great, Equal, Less

  // Other names for the same wires on the sheet: X0[3:0] = X[3:0]; X1[3:0] = X[7:4]; Y0[3:0] = Y[3:0];
  //   Y1[3:0] = Y[7:4]

  // Notes on the sheet:
  //   电路功能：X,Y进行无符号比较，Great=(X>Y)?1:0;
  //   输入引脚区
  //   输出引脚区
endmodule

// MUX
module \_2路选择器_1位  (
  input  X0,
  input  Sel,
  input  X1,
  output Out
);


  // Notes on the sheet:
  //   输入引脚区
  //   电路功能：Out=(Sel==0)?X0:X1;
  //   请勿增删改引脚，请在下方利用上方输入输出引脚的隧道标签信号构建电路，ctrl+d复制选择组件
  //   输出引脚区
endmodule

// MUX
module \_2路选择器_8位  (
  input  [7:0] X,
  input  Sel,
  input  [7:0] Y,
  output [7:0] Out
);

  // Probe on X
  // Probe on Y
  // Probe on Out

  // Notes on the sheet:
  //   输入引脚区
  //   电路功能：Out=(Sel==0)?X:Y;
  //   请勿增删改引脚，请在下方利用上方输入输出引脚的隧道标签信号构建电路，ctrl+d复制选择组件
  //   输出引脚区
endmodule

// 计数器
module \BCD双向计数器_可异步置位  (
  input  CLK,
  input  \使能 ,
  input  \异步置位控制 ,
  input  [3:0] \异步预置 ,
  input  \Mode_1正计数_0倒计数 ,
  output [3:0] \输出Q ,
  output \进位_借位 
);

  wire D0, D1, D2, D3, undriven;

  \BCD双向计数器状态转换_自动生成  \bcd双向计数器状态转换_自动生成_1  ();  // open: S3, N3, S2, N2, S1, N1, S0, N0, Mode
  \BCD双向计数器输出函数_自动生成  \bcd双向计数器输出函数_自动生成_1  (.Cout(\进位_借位 ));  // open: S3, S2, S1, S0, Mode
  assign {D3, D2, D1, D0} = \异步置位控制  ? \异步预置  : 4'bz;  // Controlled_Buffer controlled_buffer_1
  D_Flip_Flop #(.trigger("rising"), .Pre_Clr_Positions("LEGACY"), .NegatePresetClear("false"), .enable("true"), .NewFFLayout("false")) u_D3 ();  // open: clk, D, Q, Qn, preset, en, reset
  D_Flip_Flop #(.trigger("rising"), .Pre_Clr_Positions("LEGACY"), .NegatePresetClear("false"), .enable("true"), .NewFFLayout("false")) u_D2 ();  // open: clk, D, Q, Qn, preset, en, reset
  D_Flip_Flop #(.trigger("rising"), .Pre_Clr_Positions("LEGACY"), .NegatePresetClear("false"), .enable("true"), .NewFFLayout("false")) u_D1 (.reset(undriven));  // open: clk, D, Q, Qn, preset, en
  D_Flip_Flop #(.trigger("rising"), .Pre_Clr_Positions("LEGACY"), .NegatePresetClear("false"), .enable("true"), .NewFFLayout("false")) u_D0 ();  // open: clk, D, Q, Qn, preset, en, reset
  // Probe on \输出Q 

  // Other names for the same wires on the sheet: Cout = \进位_借位 ; Din[3:0] = \异步预置 ; En = \使能 ;
  //   Mode = \Mode_1正计数_0倒计数 ; PreSet = \异步置位控制 ; Q[3:0] = \输出Q 

  // Notes on the sheet:
  //   正计数到9，倒计数到0时输出为1
endmodule

// 状态转换
module \BCD双向计数器状态转换_自动生成  (
  input  S3,
  input  S2,
  input  S1,
  input  S0,
  input  Mode,
  output N3,
  output N2,
  output N1,
  output N0
);
endmodule

module \BCD双向计数器输出函数_自动生成  (
  input  S3,
  input  S2,
  input  S1,
  input  S0,
  input  Mode,
  output Cout
);
endmodule

// 倒计数
module \双位十进制双向计数器  (
  input  CLK,
  input  \使能 ,
  input  \异步置位控制 ,
  input  [7:0] \异步预置 ,
  input  \Mode_1正计数_0倒计数 ,
  output [7:0] Q,
  output \进位_借位 
);

  \BCD双向计数器_可异步置位  \bcd双向计数器_可异步置位_1  ();  // open: CLK, 使能, 异步置位控制, 异步预置, Mode_1正计数_0倒计数, 输出Q, 进位_借位
  \BCD双向计数器_可异步置位  \bcd双向计数器_可异步置位_2  ();  // open: CLK, 使能, 异步置位控制, 异步预置, Mode_1正计数_0倒计数, 输出Q, 进位_借位
  // Probe on Q

  // Other names for the same wires on the sheet: Cout = \进位_借位 ; Din[7:0] = \异步预置 ; Din0[3:0] = \异步预置 [3:0];
  //   Din1[3:0] = \异步预置 [7:4]; En = \使能 ; Mode = \Mode_1正计数_0倒计数 ; PreSet = \异步置位控制 

  // Notes on the sheet:
  //   正计数到9，倒计数到0时输出为1
endmodule

// 状态机
module \红绿灯状态机_自动生成  (
  input  S2,
  input  S1,
  input  S0,
  input  T1,
  input  T2,
  input  T3,
  input  T4,
  input  EMERG,
  output N2,
  output N1,
  output N0
);
endmodule

// 输出函数
module \红绿灯状态输出函数_真值表  (
  input  S2,
  input  S1,
  input  S0,
  output R1,
  output Y1,
  output G1,
  output R2,
  output Y2,
  output G2,
  output PASS1,
  output PASS2
);
endmodule

module \红绿灯  (
  input  in_1,
  output R1,
  output Y1,
  output [2:0] Status,
  output G1,
  output R2,
  output Y2,
  output [7:0] Timer,
  output G2
);

  wire CLK, PASS1, RST, T1, T2, undriven_2, Y1c, Y2c, \紧急开关_p1 , \紧急开关_p3 , \紧急开关_p7 , \紧急情况 ;
  wire [2:0] S1B, S2B;
  wire [3:0] S1T, S2T;
  wire [7:0] counter_1_q, Timer1, undriven;

  LED #(.active("true")) led_1 (.in(R1));
  LED #(.active("true")) led_2 (.in(Y1c));
  LED #(.active("true")) led_3 (.in(G1));
  _7_Segment_Display #(.active("true")) u_7_segment_display_1 (
    .g(S1T[0]), .f(S1T[1]), .a(S1T[2]), .b(S1T[3]), .e(S1B[0]), .d(S1B[1]), .c(S1B[2]));  // open: dp
  _7_Segment_Display #(.active("true")) u_7_segment_display_2 (
    .g(S2T[0]), .f(S2T[1]), .a(S2T[2]), .b(S2T[3]), .e(S2B[0]), .d(S2B[1]), .c(S2B[2]));  // open: dp
  Register #(.width(3), .trigger("rising"), .Select("low")) \u_状态  (.Q(Status), .clk(CLK));  // open: D, en, clr
  \双位十进制双向计数器  \u_双位十进制双向计数器_1  (
    .CLK(CLK), .\使能 (1'b1), .\异步预置 (8'h20), .Q(Timer1));  // open: 异步置位控制, Mode_1正计数_0倒计数, 进位_借位
  // DipSwitch #(.NSwitches(1)) 紧急开关: pin names not known; wires that end beside it: \紧急开关_p1 , \紧急开关_p1 , \紧急开关_p3 , R1, Y1, G1, \紧急开关_p7 , \紧急开关_p7 , R2, Y2, G2, PASS1
  \红绿灯状态输出函数_真值表  \u_红绿灯状态输出函数_真值表_1  ();  // open: S2, R1, S1, Y1, S0, G1, R2, Y2, G2, PASS1, PASS2
  // Probe on Timer1
  LED #(.active("true")) led_4 (.in(R2));
  LED #(.active("true")) led_5 (.in(Y2c));
  LED #(.active("true")) led_6 (.in(G2));
  or or_1 (\紧急情况 , in_1, \紧急开关_p3 );
  \红绿灯状态机_自动生成  \u_红绿灯状态机_自动生成_1  ();  // open: S2, N2, S1, N1, S0, N0, T1, T2, T3, T4, EMERG
  \_8位无符号比较器  \u_8位无符号比较器_1  (.X(Timer1), .Y(8'h4), .Equal(T1));  // open: Great, Less
  \_8位无符号比较器  \u_8位无符号比较器_2  (.X(Timer1), .Y(8'h1), .Equal(T2));  // open: Great, Less
  and and_1 (Y1c, Y1, CLK);
  and and_2 (Y2c, Y2, CLK);
  Clock #(.highDuration(1), .lowDuration(1)) clock_1 (.out(CLK));
  \_2路选择器_8位  \u_2路选择器_8位_1  (.X(Timer1), .Sel(undriven_2), .Y(undriven), .Out(Timer));
  D_Flip_Flop #(.trigger("rising"), .Pre_Clr_Positions("LEGACY"), .NegatePresetClear("false"), .enable("true"), .NewFFLayout("false")) d_ff_1 (
    .clk(CLK), .D(1'b1), .Qn(RST));  // open: Q, preset, en, reset
  Counter #(.width(8), .max('hff), .ongoal("wrap"), .trigger("rising"), .behavior("new")) counter_1 (
    .Q(counter_1_q), .clk(CLK));  // open: load, D, count, carry, clr, preset, down
  // Probe on counter_1_q
  \数码管驱动  \u_数码管驱动_1  (
    .X3(Timer[7]), .Seg_1(S2T[0]), .X2(Timer[6]), .Seg_2(S2T[1]), .X1(Timer[5]), .Seg_3(S2T[2]),
    .X0(Timer[4]), .Seg_4(S2T[3]), .Seg_5(S2B[0]), .Seg_6(S2B[1]), .Seg_7(S2B[2]));
  \数码管驱动  \u_数码管驱动_2  (
    .X3(Timer[3]), .Seg_1(S1T[0]), .X2(Timer[2]), .Seg_2(S1T[1]), .X1(Timer[1]), .Seg_3(S1T[2]),
    .X0(Timer[0]), .Seg_4(S1T[3]), .Seg_5(S1B[0]), .Seg_6(S1B[1]), .Seg_7(S1B[2]));

  // Other names for the same wires on the sheet: E = in_1

  // Notes on the sheet:
  //   主道红绿灯
  //   测试时要求主道20秒，辅道10秒
  //   倒计时
  //   状态机现态
  //   主道计时逻辑
  //   辅道红绿灯
  //   状态机现态
  //   当前倒计时
  //   引脚区，用于EduCoder测试
  //   控制黄灯闪烁
  //   初始化信号，第一拍为1
  //   用于预置计数器初始值
  //   当前倒计时
  //   时钟计数
endmodule
